// Logisim project 2.2-计数器.circ as structural Verilog: 3 circuits, main circuit main
module main (
);

  wire clock_1_out, count_pro_1_led;
  wire [3:0] count_pro_1_oh, count_pro_1_ol;

  Clock clock_1 (.out(clock_1_out));
  LED led_1 (.in(count_pro_1_led));
  count_pro count_pro_1 (.cp(clock_1_out), .LED(count_pro_1_led), .oH(count_pro_1_oh), .ol(count_pro_1_ol));
  Hex_Digit_Display hex_digit_display_1 (.value(count_pro_1_oh));  // open: dp
  Hex_Digit_Display hex_digit_display_2 (.value(count_pro_1_ol));  // open: dp
endmodule

module count13 (
  input  cp,
  output cout,
  output Q0,
  output Q1,
  output Q2,
  output Q3
);

  wire and_1_out, and_2_out, not_1_out, or_1_out;

  J_K_Flip_Flop j_k_ff_1 (.J(not_1_out), .K(1'b1), .clk(cp), .Q(Q0));  // open: Qn, preset, reset
  J_K_Flip_Flop j_k_ff_2 (.J(Q0), .K(Q0), .clk(cp), .Q(Q1));  // open: Qn, preset, reset
  and and_1 (and_1_out, Q0, Q1);
  or or_1 (or_1_out, and_1_out, Q3);
  J_K_Flip_Flop j_k_ff_3 (.J(and_1_out), .K(or_1_out), .clk(cp), .Q(Q2));  // open: Qn, preset, reset
  and and_2 (and_2_out, and_1_out, Q2);
  J_K_Flip_Flop j_k_ff_4 (.J(and_2_out), .K(Q2), .clk(cp), .Q(Q3));  // open: Qn, preset, reset
  and and_3 (cout, Q2, Q3);
  not not_1 (not_1_out, cout);
endmodule

module count_pro (
  input  cp,
  output LED,
  output [3:0] oH,
  output [3:0] ol
);

  wire and_1_out, count13_1_cout, count13_2_cout, d_ff_1_q, not_1_out, not_2_out, not_3_out;

  not not_1 (not_1_out, LED);
  and and_1 (and_1_out, cp, not_1_out);
  not not_2 (not_2_out, count13_1_cout);
  count13 count13_1 (.cp(and_1_out), .cout(count13_1_cout), .Q0(ol[0]), .Q1(ol[1]), .Q2(ol[2]), .Q3(ol[3]));
  D_Flip_Flop d_ff_1 (.D(and_1_out), .clk(not_2_out), .Q(d_ff_1_q), .reset(ol[0]));  // open: Qn, preset
  count13 count13_2 (.cp(d_ff_1_q), .cout(count13_2_cout), .Q0(oH[0]), .Q1(oH[1]), .Q2(oH[2]), .Q3(oH[3]));
  not not_3 (not_3_out, count13_2_cout);
  D_Flip_Flop d_ff_2 (.D(d_ff_1_q), .clk(not_3_out), .Q(LED));  // open: Qn, preset, reset
endmodule
