// Logisim project 2.3-乘法器.circ as structural Verilog: 6 circuits, main circuit main
module main (
  input  [7:0] a,
  input  in_2,
  input  [7:0] b
);

  wire clock_1_out;
  wire [3:0] muti_1_count;
  wire [7:0] muti_1_product;

  Clock clock_1 (.out(clock_1_out));
  muti muti_1 (
    .muti_op1(a), .reset(in_2), .cp(clock_1_out), .muti_op2(b), .product(muti_1_product), .count(muti_1_count));
  Hex_Digit_Display hex_digit_display_1 (.value(muti_1_count));  // open: dp
  Hex_Digit_Display hex_digit_display_2 (.value(muti_1_product[7:4]));  // open: dp
  Hex_Digit_Display hex_digit_display_3 (.value(muti_1_product[3:0]));  // open: dp
endmodule

module Add_1 (
  input  A,
  input  B,
  input  C,
  output S,
  output cout
);

  wire and_1_out, and_2_out, or_1_out, xor_1_out;

  xor xor_1 (xor_1_out, A, B);
  or or_1 (or_1_out, B, C);
  and and_1 (and_1_out, C, B);
  xor xor_2 (S, xor_1_out, C);
  and and_2 (and_2_out, A, or_1_out);
  or or_2 (cout, and_2_out, and_1_out);
endmodule

module Add_7 (
  input  [6:0] a0,
  input  [6:0] b0,
  output [6:0] out_3,
  output cout
);

  wire add_1_1_cout, add_1_2_cout, add_1_3_cout, add_1_4_cout, add_1_5_cout, add_1_6_cout;

  Add_1 add_1_1 (.A(a0[0]), .B(b0[0]), .C(1'b0), .S(out_3[0]), .cout(add_1_1_cout));
  Add_1 add_1_2 (.A(a0[1]), .B(b0[1]), .C(add_1_1_cout), .S(out_3[1]), .cout(add_1_2_cout));
  Add_1 add_1_3 (.A(a0[2]), .B(b0[2]), .C(add_1_2_cout), .S(out_3[2]), .cout(add_1_3_cout));
  Add_1 add_1_4 (.A(a0[3]), .B(b0[3]), .C(add_1_3_cout), .S(out_3[3]), .cout(add_1_4_cout));
  Add_1 add_1_5 (.A(a0[4]), .B(b0[4]), .C(add_1_4_cout), .S(out_3[4]), .cout(add_1_5_cout));
  Add_1 add_1_6 (.A(a0[5]), .B(b0[5]), .C(add_1_5_cout), .S(out_3[5]), .cout(add_1_6_cout));
  Add_1 add_1_7 (.A(a0[6]), .B(b0[6]), .C(add_1_6_cout), .S(out_3[6]), .cout(cout));
endmodule

module shift (
  input  [7:0] a0,
  output [7:0] out_2
);

  wire [6:0] adder_1_out, not_1_out;

  not not_1 (not_1_out[0], a0[0]);
  not not_2 (not_1_out[1], a0[1]);
  not not_3 (not_1_out[2], a0[2]);
  not not_4 (not_1_out[3], a0[3]);
  not not_5 (not_1_out[4], a0[4]);
  not not_6 (not_1_out[5], a0[5]);
  not not_7 (not_1_out[6], a0[6]);
  Multiplexer #(.width(7)) multiplexer_1 (.in0(a0[6:0]), .in1(adder_1_out), .out(out_2[6:0]), .sel(a0[7]));
  Adder #(.width(7)) adder_1 (.a(not_1_out), .b(7'b0000001), .out(adder_1_out));  // open: cin, cout

  assign out_2[7] = a0[7];
endmodule

module muti (
  input  [7:0] muti_op1,
  input  reset,
  input  cp,
  input  [7:0] muti_op2,
  output [7:0] product,
  output [3:0] count
);

  wire and_1_out, comparator_1_eq, comparator_2_gt, not_1_out;
  wire [0:0] add_7_1_out_3;
  wire [6:0] add_7_1_cout, multiplexer_1_out, multiplexer_2_out, register_1_q;
  wire [7:0] control_1_product, register_2_q, shift_1_out_2, shift_2_out_2, shift_3_out_2;

  not not_1 (not_1_out, comparator_2_gt);
  and and_1 (and_1_out, not_1_out, cp);
  shift shift_1 (.a0(muti_op1), .out_2(shift_1_out_2));
  shift shift_2 (.a0(muti_op2), .out_2(shift_2_out_2));
  xor xor_1 (register_2_q[7], shift_1_out_2[7], shift_2_out_2[7]);
  Multiplexer #(.width(7)) multiplexer_1 (
    .in0({7{1'b0}}), .in1(shift_1_out_2[6:0]), .out(multiplexer_1_out), .sel(register_2_q[0]));
  Register #(.width(7)) register_1 (.D(add_7_1_cout), .en(not_1_out), .clk(and_1_out), .Q(register_1_q), .clr(reset));
  Multiplexer #(.width(7)) multiplexer_2 (
    .in0({add_7_1_out_3[0], register_2_q[6:1]}), .in1(shift_2_out_2[6:0]), .out(multiplexer_2_out),
    .sel(comparator_1_eq));
  Register #(.width(7)) register_2 (
    .D(multiplexer_2_out), .en(not_1_out), .clk(and_1_out), .Q(register_2_q[6:0]), .clr(reset));
  Add_7 add_7_1 (
    .a0(multiplexer_1_out), .b0(register_1_q), .out_3({add_7_1_cout[5:0], add_7_1_out_3[0]}),
    .cout(add_7_1_cout[6]));
  Counter #(.max('h8), .ongoal("stay"), .width(4)) counter_1 (
    .count(1'b1), .Q(count), .up(1'b1), .clk(and_1_out), .clr(reset));  // open: load, D, carry
  Comparator #(.mode("unsigned"), .width(4)) comparator_1 (
    .a(count), .b(4'b0000), .eq(comparator_1_eq));  // open: gt, lt
  Comparator #(.mode("unsigned"), .width(4)) comparator_2 (
    .a(count), .b(4'b0111), .gt(comparator_2_gt));  // open: eq, lt
  control control_1 (.res(register_2_q), .cin(count), .product(control_1_product));
  shift shift_3 (.a0(control_1_product), .out_2(shift_3_out_2));
  Multiplexer #(.width(8)) multiplexer_3 (
    .in0(control_1_product), .in1(shift_3_out_2), .out(product), .sel(comparator_2_gt));
endmodule

module control (
  input  [7:0] res,
  input  [3:0] cin,
  output [7:0] product
);

  wire not_1_out, or_1_out;

  not not_1 (not_1_out, cin[3]);
  or or_1 (or_1_out, cin[0], cin[1], cin[2], not_1_out);
  or or_2 (product[0], res[0], or_1_out);
  or or_3 (product[1], res[1], or_1_out);
  or or_4 (product[2], res[2], or_1_out);
  or or_5 (product[3], res[3], or_1_out);
  or or_6 (product[4], res[4], or_1_out);
  or or_7 (product[5], res[5], or_1_out);
  or or_8 (product[6], res[6], or_1_out);
  or or_9 (product[7], res[7], or_1_out);
endmodule
