// Logisim project 3.1-寄存器堆.circ as structural Verilog: 4 circuits, main circuit main
module main (
  input  in_1,
  input  [4:0] in_2,
  input  [31:0] in_3,
  input  [4:0] in_4,
  input  [4:0] in_5
);

  wire clock_1_out;
  wire [31:0] mips_32x32_reg_1_rdata1, mips_32x32_reg_1_rdata2;

  Clock clock_1 (.out(clock_1_out));
  MIPS_32x32_reg mips_32x32_reg_1 (
    .cp(clock_1_out), .wen(in_1), .waddr(in_2), .wdata(in_3), .raddr1(in_4), .raddr2(in_5),
    .rdata1(mips_32x32_reg_1_rdata1), .rdata2(mips_32x32_reg_1_rdata2));
  Hex_Digit_Display hex_digit_display_1 (.value(mips_32x32_reg_1_rdata1[31:28]));  // open: dp
  Hex_Digit_Display hex_digit_display_2 (.value(mips_32x32_reg_1_rdata1[27:24]));  // open: dp
  Hex_Digit_Display hex_digit_display_3 (.value(mips_32x32_reg_1_rdata1[23:20]));  // open: dp
  Hex_Digit_Display hex_digit_display_4 (.value(mips_32x32_reg_1_rdata2[31:28]));  // open: dp
  Hex_Digit_Display hex_digit_display_5 (.value(mips_32x32_reg_1_rdata2[27:24]));  // open: dp
  Hex_Digit_Display hex_digit_display_6 (.value(mips_32x32_reg_1_rdata1[19:16]));  // open: dp
  Hex_Digit_Display hex_digit_display_7 (.value(mips_32x32_reg_1_rdata1[15:12]));  // open: dp
  Hex_Digit_Display hex_digit_display_8 (.value(mips_32x32_reg_1_rdata2[23:20]));  // open: dp
  Hex_Digit_Display hex_digit_display_9 (.value(mips_32x32_reg_1_rdata2[19:16]));  // open: dp
  Hex_Digit_Display hex_digit_display_10 (.value(mips_32x32_reg_1_rdata1[11:8]));  // open: dp
  Hex_Digit_Display hex_digit_display_11 (.value(mips_32x32_reg_1_rdata1[7:4]));  // open: dp
  Hex_Digit_Display hex_digit_display_12 (.value(mips_32x32_reg_1_rdata2[15:12]));  // open: dp
  Hex_Digit_Display hex_digit_display_13 (.value(mips_32x32_reg_1_rdata2[11:8]));  // open: dp
  Hex_Digit_Display hex_digit_display_14 (.value(mips_32x32_reg_1_rdata1[3:0]));  // open: dp
  Hex_Digit_Display hex_digit_display_15 (.value(mips_32x32_reg_1_rdata2[3:0]));  // open: dp
  Hex_Digit_Display hex_digit_display_16 (.value(mips_32x32_reg_1_rdata2[7:4]));  // open: dp
endmodule

module group_0 (
  input  cp,
  input  group_en,
  input  [31:0] wdata,
  input  [2:0] inner_waddr,
  output [31:0] reg_0,
  output [31:0] reg_1,
  output [31:0] reg_2,
  output [31:0] reg_3,
  output [31:0] reg_4,
  output [31:0] reg_5,
  output [31:0] reg_6,
  output [31:0] reg_7
);

  wire and_1_out, and_2_out, and_3_out, and_4_out, and_5_out, and_6_out, and_7_out, not_1_out, not_2_out,
       not_3_out, not_4_out, not_5_out, not_6_out, not_7_out, not_8_out, not_9_out;
  wire [31:0] multiplexer_1_out, multiplexer_2_out, multiplexer_3_out, multiplexer_4_out, multiplexer_5_out,
       multiplexer_6_out, multiplexer_7_out;

  Multiplexer #(.width(32)) multiplexer_1 (.in0(reg_1), .in1(wdata), .out(multiplexer_1_out), .sel(and_1_out));
  Multiplexer #(.width(32)) multiplexer_2 (.in0(reg_2), .in1(wdata), .out(multiplexer_2_out), .sel(and_2_out));
  Multiplexer #(.width(32)) multiplexer_3 (.in0(reg_3), .in1(wdata), .out(multiplexer_3_out), .sel(and_3_out));
  Multiplexer #(.width(32)) multiplexer_4 (.in0(reg_4), .in1(wdata), .out(multiplexer_4_out), .sel(and_4_out));
  Multiplexer #(.width(32)) multiplexer_5 (.in0(reg_5), .in1(wdata), .out(multiplexer_5_out), .sel(and_5_out));
  Multiplexer #(.width(32)) multiplexer_6 (.in0(reg_6), .in1(wdata), .out(multiplexer_6_out), .sel(and_6_out));
  Multiplexer #(.width(32)) multiplexer_7 (.in0(reg_7), .in1(wdata), .out(multiplexer_7_out), .sel(and_7_out));
  not not_1 (not_1_out, inner_waddr[1]);
  not not_2 (not_2_out, inner_waddr[2]);
  not not_3 (not_3_out, inner_waddr[0]);
  not not_4 (not_4_out, inner_waddr[2]);
  not not_5 (not_5_out, inner_waddr[2]);
  not not_6 (not_6_out, inner_waddr[0]);
  not not_7 (not_7_out, inner_waddr[1]);
  not not_8 (not_8_out, inner_waddr[1]);
  not not_9 (not_9_out, inner_waddr[0]);
  and and_1 (and_1_out, inner_waddr[0], not_1_out, not_2_out);
  and and_2 (and_2_out, not_3_out, inner_waddr[1], not_4_out);
  and and_3 (and_3_out, inner_waddr[0], inner_waddr[1], not_5_out);
  and and_4 (and_4_out, not_6_out, not_7_out, inner_waddr[2]);
  and and_5 (and_5_out, inner_waddr[0], not_8_out, inner_waddr[2]);
  and and_6 (and_6_out, not_9_out, inner_waddr[1], inner_waddr[2]);
  and and_7 (and_7_out, inner_waddr[0], inner_waddr[1], inner_waddr[2]);
  Register #(.width(32)) register_1 (.D({32{1'b0}}), .en(group_en), .clk(cp), .Q(reg_0));  // open: clr
  Register #(.width(32)) register_2 (.D(multiplexer_1_out), .en(group_en), .clk(cp), .Q(reg_1));  // open: clr
  Register #(.width(32)) register_3 (.D(multiplexer_2_out), .en(group_en), .clk(cp), .Q(reg_2));  // open: clr
  Register #(.width(32)) register_4 (.D(multiplexer_3_out), .en(group_en), .clk(cp), .Q(reg_3));  // open: clr
  Register #(.width(32)) register_5 (.D(multiplexer_4_out), .en(group_en), .clk(cp), .Q(reg_4));  // open: clr
  Register #(.width(32)) register_6 (.D(multiplexer_5_out), .en(group_en), .clk(cp), .Q(reg_5));  // open: clr
  Register #(.width(32)) register_7 (.D(multiplexer_6_out), .en(group_en), .clk(cp), .Q(reg_6));  // open: clr
  Register #(.width(32)) register_8 (.D(multiplexer_7_out), .en(group_en), .clk(cp), .Q(reg_7));  // open: clr
endmodule

module MIPS_32x32_reg (
  input  cp,
  input  wen,
  input  [4:0] waddr,
  input  [31:0] wdata,
  input  [4:0] raddr1,
  input  [4:0] raddr2,
  output [31:0] rdata1,
  output [31:0] rdata2
);

  wire and_1_out, and_2_out, and_3_out, and_4_out, not_1_out, not_2_out, not_3_out, not_4_out;
  wire [31:0] group_0_1_reg_0, group_0_1_reg_1, group_0_1_reg_2, group_0_1_reg_3, group_0_1_reg_4,
       group_0_1_reg_5, group_0_1_reg_6, group_0_1_reg_7, group_123_1_reg_0, group_123_1_reg_1,
       group_123_1_reg_2, group_123_1_reg_3, group_123_1_reg_4, group_123_1_reg_5, group_123_1_reg_6,
       group_123_1_reg_7, group_123_2_reg_0, group_123_2_reg_1, group_123_2_reg_2, group_123_2_reg_3,
       group_123_2_reg_4, group_123_2_reg_5, group_123_2_reg_6, group_123_2_reg_7, group_123_3_reg_0,
       group_123_3_reg_1, group_123_3_reg_2, group_123_3_reg_3, group_123_3_reg_4, group_123_3_reg_5,
       group_123_3_reg_6, group_123_3_reg_7, multiplexer_1_out, multiplexer_2_out, multiplexer_3_out,
       multiplexer_4_out, multiplexer_5_out, multiplexer_6_out, multiplexer_7_out, multiplexer_8_out;

  not not_1 (not_1_out, waddr[3]);
  and and_1 (and_1_out, wen, not_1_out, not_2_out);
  not not_2 (not_2_out, waddr[4]);
  and and_2 (and_2_out, wen, waddr[3], not_3_out);
  not not_3 (not_3_out, waddr[4]);
  not not_4 (not_4_out, waddr[3]);
  and and_3 (and_3_out, wen, not_4_out, waddr[4]);
  and and_4 (and_4_out, waddr[3], waddr[4], wen);
  group_0 group_0_1 (
    .cp(cp), .group_en(and_1_out), .wdata(wdata), .inner_waddr(waddr[2:0]), .reg_0(group_0_1_reg_0),
    .reg_1(group_0_1_reg_1), .reg_2(group_0_1_reg_2), .reg_3(group_0_1_reg_3), .reg_4(group_0_1_reg_4),
    .reg_5(group_0_1_reg_5), .reg_6(group_0_1_reg_6), .reg_7(group_0_1_reg_7));
  group_123 group_123_1 (
    .cp(cp), .group_en(and_2_out), .wdata(wdata), .inner_waddr(waddr[2:0]), .reg_0(group_123_1_reg_0),
    .reg_1(group_123_1_reg_1), .reg_2(group_123_1_reg_2), .reg_3(group_123_1_reg_3),
    .reg_4(group_123_1_reg_4), .reg_5(group_123_1_reg_5), .reg_6(group_123_1_reg_6), .reg_7(group_123_1_reg_7));
  group_123 group_123_2 (
    .cp(cp), .group_en(and_3_out), .wdata(wdata), .inner_waddr(waddr[2:0]), .reg_0(group_123_2_reg_0),
    .reg_1(group_123_2_reg_1), .reg_2(group_123_2_reg_2), .reg_3(group_123_2_reg_3),
    .reg_4(group_123_2_reg_4), .reg_5(group_123_2_reg_5), .reg_6(group_123_2_reg_6), .reg_7(group_123_2_reg_7));
  group_123 group_123_3 (
    .cp(cp), .group_en(and_4_out), .wdata(wdata), .inner_waddr(waddr[2:0]), .reg_0(group_123_3_reg_0),
    .reg_1(group_123_3_reg_1), .reg_2(group_123_3_reg_2), .reg_3(group_123_3_reg_3),
    .reg_4(group_123_3_reg_4), .reg_5(group_123_3_reg_5), .reg_6(group_123_3_reg_6), .reg_7(group_123_3_reg_7));
  Multiplexer #(.select(3), .width(32)) multiplexer_1 (
    .in0(group_0_1_reg_0), .in1(group_0_1_reg_1), .in2(group_0_1_reg_2), .in3(group_0_1_reg_3),
    .in4(group_0_1_reg_4), .in5(group_0_1_reg_5), .in6(group_0_1_reg_6), .in7(group_0_1_reg_7),
    .out(multiplexer_1_out), .sel(raddr1[2:0]));
  Multiplexer #(.select(3), .width(32)) multiplexer_2 (
    .in0(group_123_1_reg_0), .in1(group_123_1_reg_1), .in2(group_123_1_reg_2), .in3(group_123_1_reg_3),
    .in4(group_123_1_reg_4), .in5(group_123_1_reg_5), .in6(group_123_1_reg_6), .in7(group_123_1_reg_7),
    .out(multiplexer_2_out), .sel(raddr1[2:0]));
  Multiplexer #(.select(3), .width(32)) multiplexer_3 (
    .in0(group_123_2_reg_0), .in1(group_123_2_reg_1), .in2(group_123_2_reg_2), .in3(group_123_2_reg_3),
    .in4(group_123_2_reg_4), .in5(group_123_2_reg_5), .in6(group_123_2_reg_6), .in7(group_123_2_reg_7),
    .out(multiplexer_3_out), .sel(raddr1[2:0]));
  Multiplexer #(.select(3), .width(32)) multiplexer_4 (
    .in0(group_123_3_reg_0), .in1(group_123_3_reg_1), .in2(group_123_3_reg_2), .in3(group_123_3_reg_3),
    .in4(group_123_3_reg_4), .in5(group_123_3_reg_5), .in6(group_123_3_reg_6), .in7(group_123_3_reg_7),
    .out(multiplexer_4_out), .sel(raddr1[2:0]));
  Multiplexer #(.select(3), .width(32)) multiplexer_5 (
    .in0(group_0_1_reg_0), .in1(group_0_1_reg_1), .in2(group_0_1_reg_2), .in3(group_0_1_reg_3),
    .in4(group_0_1_reg_4), .in5(group_0_1_reg_5), .in6(group_0_1_reg_6), .in7(group_0_1_reg_7),
    .out(multiplexer_5_out), .sel(raddr2[2:0]));
  Multiplexer #(.select(3), .width(32)) multiplexer_6 (
    .in0(group_123_1_reg_0), .in1(group_123_1_reg_1), .in2(group_123_1_reg_2), .in3(group_123_1_reg_3),
    .in4(group_123_1_reg_4), .in5(group_123_1_reg_5), .in6(group_123_1_reg_6), .in7(group_123_1_reg_7),
    .out(multiplexer_6_out), .sel(raddr2[2:0]));
  Multiplexer #(.select(3), .width(32)) multiplexer_7 (
    .in0(group_123_2_reg_0), .in1(group_123_2_reg_1), .in2(group_123_2_reg_2), .in3(group_123_2_reg_3),
    .in4(group_123_2_reg_4), .in5(group_123_2_reg_5), .in6(group_123_2_reg_6), .in7(group_123_2_reg_7),
    .out(multiplexer_7_out), .sel(raddr2[2:0]));
  Multiplexer #(.select(3), .width(32)) multiplexer_8 (
    .in0(group_123_3_reg_0), .in1(group_123_3_reg_1), .in2(group_123_3_reg_2), .in3(group_123_3_reg_3),
    .in4(group_123_3_reg_4), .in5(group_123_3_reg_5), .in6(group_123_3_reg_6), .in7(group_123_3_reg_7),
    .out(multiplexer_8_out), .sel(raddr2[2:0]));
  Multiplexer #(.select(2), .width(32)) multiplexer_9 (
    .in0(multiplexer_1_out), .in1(multiplexer_2_out), .in2(multiplexer_3_out), .in3(multiplexer_4_out),
    .out(rdata1), .sel(raddr1[4:3]));
  Multiplexer #(.select(2), .width(32)) multiplexer_10 (
    .in0(multiplexer_5_out), .in1(multiplexer_6_out), .in2(multiplexer_7_out), .in3(multiplexer_8_out),
    .out(rdata2), .sel(raddr2[4:3]));
endmodule

module group_123 (
  input  cp,
  input  group_en,
  input  [31:0] wdata,
  input  [2:0] inner_waddr,
  output [31:0] reg_0,
  output [31:0] reg_1,
  output [31:0] reg_2,
  output [31:0] reg_3,
  output [31:0] reg_4,
  output [31:0] reg_5,
  output [31:0] reg_6,
  output [31:0] reg_7
);

  wire and_1_out, and_2_out, and_3_out, and_4_out, and_5_out, and_6_out, and_7_out, and_8_out, not_1_out,
       not_2_out, not_3_out, not_4_out, not_5_out, not_6_out, not_7_out, not_8_out, not_9_out, not_10_out,
       not_11_out, not_12_out;
  wire [31:0] multiplexer_1_out, multiplexer_2_out, multiplexer_3_out, multiplexer_4_out, multiplexer_5_out,
       multiplexer_6_out, multiplexer_7_out, multiplexer_8_out;

  Multiplexer #(.width(32)) multiplexer_1 (.in0(reg_0), .in1(wdata), .out(multiplexer_1_out), .sel(and_1_out));
  Multiplexer #(.width(32)) multiplexer_2 (.in0(reg_1), .in1(wdata), .out(multiplexer_2_out), .sel(and_2_out));
  Multiplexer #(.width(32)) multiplexer_3 (.in0(reg_2), .in1(wdata), .out(multiplexer_3_out), .sel(and_3_out));
  Multiplexer #(.width(32)) multiplexer_4 (.in0(reg_3), .in1(wdata), .out(multiplexer_4_out), .sel(and_4_out));
  Multiplexer #(.width(32)) multiplexer_5 (.in0(reg_4), .in1(wdata), .out(multiplexer_5_out), .sel(and_5_out));
  Multiplexer #(.width(32)) multiplexer_6 (.in0(reg_5), .in1(wdata), .out(multiplexer_6_out), .sel(and_6_out));
  Multiplexer #(.width(32)) multiplexer_7 (.in0(reg_6), .in1(wdata), .out(multiplexer_7_out), .sel(and_7_out));
  Multiplexer #(.width(32)) multiplexer_8 (.in0(reg_7), .in1(wdata), .out(multiplexer_8_out), .sel(and_8_out));
  not not_1 (not_1_out, inner_waddr[0]);
  not not_2 (not_2_out, inner_waddr[1]);
  not not_3 (not_3_out, inner_waddr[2]);
  not not_4 (not_4_out, inner_waddr[1]);
  not not_5 (not_5_out, inner_waddr[2]);
  not not_6 (not_6_out, inner_waddr[0]);
  not not_7 (not_7_out, inner_waddr[2]);
  not not_8 (not_8_out, inner_waddr[2]);
  not not_9 (not_9_out, inner_waddr[1]);
  not not_10 (not_10_out, inner_waddr[0]);
  and and_1 (and_1_out, not_1_out, not_2_out, not_3_out);
  and and_2 (and_2_out, inner_waddr[0], not_4_out, not_5_out);
  and and_3 (and_3_out, not_6_out, inner_waddr[1], not_7_out);
  and and_4 (and_4_out, inner_waddr[0], inner_waddr[1], not_8_out);
  not not_11 (not_11_out, inner_waddr[0]);
  not not_12 (not_12_out, inner_waddr[1]);
  and and_5 (and_5_out, not_11_out, not_12_out, inner_waddr[2]);
  and and_6 (and_6_out, inner_waddr[0], not_9_out, inner_waddr[2]);
  and and_7 (and_7_out, not_10_out, inner_waddr[1], inner_waddr[2]);
  and and_8 (and_8_out, inner_waddr[0], inner_waddr[1], inner_waddr[2]);
  Register #(.width(32)) register_1 (.D(multiplexer_1_out), .en(group_en), .clk(cp), .Q(reg_0));  // open: clr
  Register #(.width(32)) register_2 (.D(multiplexer_2_out), .en(group_en), .clk(cp), .Q(reg_1));  // open: clr
  Register #(.width(32)) register_3 (.D(multiplexer_3_out), .en(group_en), .clk(cp), .Q(reg_2));  // open: clr
  Register #(.width(32)) register_4 (.D(multiplexer_4_out), .en(group_en), .clk(cp), .Q(reg_3));  // open: clr
  Register #(.width(32)) register_5 (.D(multiplexer_5_out), .en(group_en), .clk(cp), .Q(reg_4));  // open: clr
  Register #(.width(32)) register_6 (.D(multiplexer_6_out), .en(group_en), .clk(cp), .Q(reg_5));  // open: clr
  Register #(.width(32)) register_7 (.D(multiplexer_7_out), .en(group_en), .clk(cp), .Q(reg_6));  // open: clr
  Register #(.width(32)) register_8 (.D(multiplexer_8_out), .en(group_en), .clk(cp), .Q(reg_7));  // open: clr
endmodule
