// Logisim project 3.2-存储器.circ as structural Verilog: 4 circuits, main circuit main
module main (
  input  [15:0] in_1,
  input  in_2,
  input  in_3,
  input  [31:0] in_4,
  input  in_5,
  input  in_6
);

  wire clock_1_out, ram_pro_1_expect;
  wire [3:0] register_1_q_2, register_1_q_3, register_1_q_4;
  wire [19:0] register_1_q;
  wire [31:0] ram_pro_1_dataout;

  Clock clock_1 (.out(clock_1_out));
  LED led_1 (.in(ram_pro_1_expect));
  RAM_pro ram_pro_1 (
    .address(in_1), .Mcontrol(in_2), .MemWrite(in_3), .Datain(in_4), .MemRead(in_5), .clk(in_6),
    .Expect(ram_pro_1_expect), .DataOut(ram_pro_1_dataout));
  Hex_Digit_Display hex_digit_display_1 (.value(register_1_q_4));  // open: dp
  Register #(.width(32)) register_1 (
    .D(ram_pro_1_dataout), .en(1'b1), .clk(clock_1_out),
    .Q({register_1_q_4, register_1_q_3, register_1_q_2, register_1_q}));  // open: clr
  Hex_Digit_Display hex_digit_display_2 (.value(register_1_q_3));  // open: dp
  Hex_Digit_Display hex_digit_display_3 (.value(register_1_q_2));  // open: dp
  Hex_Digit_Display hex_digit_display_4 (.value(register_1_q[19:16]));  // open: dp
  Hex_Digit_Display hex_digit_display_5 (.value(register_1_q[15:12]));  // open: dp
  Hex_Digit_Display hex_digit_display_6 (.value(register_1_q[11:8]));  // open: dp
  Hex_Digit_Display hex_digit_display_7 (.value(register_1_q[7:4]));  // open: dp
  Hex_Digit_Display hex_digit_display_8 (.value(register_1_q[3:0]));  // open: dp
endmodule

module ROM_64KB_32bit (
  input  [15:0] address_byte,
  input  enable,
  input  cp
);

  wire [3:0] register_1_q_2, register_1_q_3, register_1_q_4;
  wire [19:0] register_1_q;
  wire [31:0] rom_1_data;

  ROM #(.addrWidth(14), .dataWidth(32)) rom_1 (.addr(address_byte[15:2]), .data(rom_1_data));
  Hex_Digit_Display hex_digit_display_1 (.value(register_1_q_4));  // open: dp
  Hex_Digit_Display hex_digit_display_2 (.value(register_1_q_3));  // open: dp
  Register #(.width(32)) register_1 (
    .D(rom_1_data), .en(enable), .clk(cp), .Q({register_1_q_4, register_1_q_3, register_1_q_2, register_1_q}));  // open: clr
  Hex_Digit_Display hex_digit_display_3 (.value(register_1_q_2));  // open: dp
  Hex_Digit_Display hex_digit_display_4 (.value(register_1_q[19:16]));  // open: dp
  Hex_Digit_Display hex_digit_display_5 (.value(register_1_q[15:12]));  // open: dp
  Hex_Digit_Display hex_digit_display_6 (.value(register_1_q[11:8]));  // open: dp
  Hex_Digit_Display hex_digit_display_7 (.value(register_1_q[7:4]));  // open: dp
  Hex_Digit_Display hex_digit_display_8 (.value(register_1_q[3:0]));  // open: dp

  // Notes on the sheet:
  //   contents of rom_1 (hex, n*v repeats v):
  //   11111111 22222222 33333333 44444444 aabbccdd ffff ffff0000 12345678 deadbeef cafebabe 88888888
  //   99999999
endmodule

module RAM_64KB_32bit (
  input  cp,
  input  [15:0] address_byte,
  input  MemWrite,
  input  MemRead,
  input  [31:0] DataIn
);

  wire not_1_out;
  wire [3:0] register_1_q_2, register_1_q_3, register_1_q_4;
  wire [19:0] register_1_q;
  wire [31:0] ram_1_dout;

  RAM #(.addrWidth(14), .asyncread("true"), .dataWidth(32)) ram_1 (
    .addr(address_byte[15:2]), .we(MemWrite), .oe(MemRead), .clk(cp), .din(DataIn), .dout(ram_1_dout));
  Register #(.width(32)) register_1 (
    .D(ram_1_dout), .en(1'b1), .clk(cp), .Q({register_1_q_4, register_1_q_3, register_1_q_2, register_1_q}),
    .clr(not_1_out));
  not not_1 (not_1_out, MemRead);
  Hex_Digit_Display hex_digit_display_1 (.value(register_1_q_4));  // open: dp
  Hex_Digit_Display hex_digit_display_2 (.value(register_1_q_3));  // open: dp
  Hex_Digit_Display hex_digit_display_3 (.value(register_1_q_2));  // open: dp
  Hex_Digit_Display hex_digit_display_4 (.value(register_1_q[19:16]));  // open: dp
  Hex_Digit_Display hex_digit_display_5 (.value(register_1_q[15:12]));  // open: dp
  Hex_Digit_Display hex_digit_display_6 (.value(register_1_q[11:8]));  // open: dp
  Hex_Digit_Display hex_digit_display_7 (.value(register_1_q[7:4]));  // open: dp
  Hex_Digit_Display hex_digit_display_8 (.value(register_1_q[3:0]));  // open: dp
endmodule

module RAM_pro (
  input  [15:0] address,
  input  Mcontrol,
  input  MemWrite,
  input  [31:0] Datain,
  input  MemRead,
  input  clk,
  output Expect,
  output [31:0] DataOut
);

  wire and_2_out, and_3_out, and_4_out, and_5_out, demultiplexer_1_out0, demultiplexer_1_out1,
       demultiplexer_1_out2, demultiplexer_1_out3, not_1_out, or_1_out, or_2_out, or_3_out, or_4_out,
       or_5_out, or_6_out;
  wire [7:0] multiplexer_1_out, multiplexer_2_out, multiplexer_3_out, multiplexer_4_out, multiplexer_5_out,
       RAM0_dout, RAM1_dout, ram_1_dout, ram_2_dout;
  wire [31:0] bit_extender_1_out;

  not not_1 (not_1_out, Mcontrol);
  or or_1 (or_1_out, address[0], address[1]);
  and and_1 (Expect, or_1_out, not_1_out);
  Demultiplexer #(.select(2)) demultiplexer_1 (
    .out0(demultiplexer_1_out0), .out1(demultiplexer_1_out1), .out2(demultiplexer_1_out2),
    .out3(demultiplexer_1_out3), .in(1'b1), .sel(address[1:0]));
  Multiplexer #(.width(8)) multiplexer_1 (
    .in0(Datain[7:0]), .in1(Datain[31:24]), .out(multiplexer_1_out), .sel(Mcontrol));
  Multiplexer #(.width(8)) multiplexer_2 (
    .in0(Datain[15:8]), .in1(Datain[31:24]), .out(multiplexer_2_out), .sel(Mcontrol));
  Multiplexer #(.width(8)) multiplexer_3 (.in0(Datain[23:16]), .out(multiplexer_3_out), .sel(Mcontrol));  // open: in1
  Multiplexer #(.width(8)) multiplexer_4 (
    .in0(Datain[31:24]), .in1(Datain[31:24]), .out(multiplexer_4_out), .sel(Mcontrol));
  or or_2 (or_2_out, not_1_out, demultiplexer_1_out0);
  or or_3 (or_3_out, not_1_out, demultiplexer_1_out1);
  or or_4 (or_4_out, not_1_out, demultiplexer_1_out2);
  or or_5 (or_5_out, not_1_out, demultiplexer_1_out3);
  and and_2 (and_2_out, or_2_out, MemWrite);
  and and_3 (and_3_out, or_3_out, MemWrite);
  and and_4 (and_4_out, or_4_out, MemWrite);
  and and_5 (and_5_out, or_5_out, MemWrite);
  RAM #(.addrWidth(14), .asyncread("true")) RAM0 (
    .addr(address[15:2]), .we(and_5_out), .oe(MemRead), .clk(clk), .din(multiplexer_1_out), .dout(RAM0_dout));
  RAM #(.addrWidth(14), .asyncread("true")) RAM1 (
    .addr(address[15:2]), .we(and_4_out), .oe(MemRead), .clk(clk), .din(multiplexer_2_out), .dout(RAM1_dout));
  RAM #(.addrWidth(14), .asyncread("true"), .clearpin("true")) ram_1 (
    .addr(address[15:2]), .we(and_3_out), .oe(MemRead), .clk(clk), .din(multiplexer_3_out), .dout(ram_1_dout));  // open: clr
  RAM #(.addrWidth(14), .asyncread("true"), .clearpin("true")) ram_2 (
    .addr(address[15:2]), .we(and_2_out), .oe(MemRead), .clk(clk), .din(multiplexer_4_out), .dout(ram_2_dout));  // open: clr
  assign bit_extender_1_out = {{24{1'b1}}, multiplexer_5_out};  // Bit_Extender bit_extender_1
  Multiplexer #(.select(2), .width(8)) multiplexer_5 (
    .in0(ram_2_dout), .in1(ram_1_dout), .in2(RAM1_dout), .in3(RAM0_dout), .out(multiplexer_5_out),
    .sel(address[1:0]));
  Multiplexer #(.width(32)) multiplexer_6 (
    .in0({ram_2_dout, ram_1_dout, RAM1_dout, RAM0_dout}), .in1(bit_extender_1_out), .out(DataOut),
    .sel(or_6_out));
  or or_6 (or_6_out, Expect, Mcontrol);

  // Notes on the sheet:
  //   高位
endmodule
