// Logisim project 4.1-单周期CPU.circ as structural Verilog: 11 circuits, main circuit main
module main (
  input  [31:0] in_1,
  input  reset,
  input  clk
);

  wire alu_1_zero, and_1_out, and_2_out, cu_1_alusrc, cu_1_branch, cu_1_extop, cu_1_memread, cu_1_memtoreg,
       cu_1_memwrite, cu_1_regdst, cu_1_regwrite, cu_1_stop, not_1_out, not_2_out, or_1_out;
  wire [2:0] alu_control_1_alucontrol, cu_1_aluop;
  wire [3:0] count_1_result, count_1_result_2, count_1_result_3, count_1_result_4;
  wire [4:0] multiplexer_2_out;
  wire [31:0] add4_1_pcout, adder_1_out, alu_1_result, ex_control_1_imm_out, mips_32x32_reg_1_rdata1,
       mips_32x32_reg_1_rdata2, multiplexer_1_out, multiplexer_3_out, multiplexer_4_out, multiplexer_5_out,
       ram_1_dout, register_1_q, rom_1_data, shift_left_2_1_out_2;

  or or_1 (or_1_out, reset, not_1_out);
  not not_1 (not_1_out, cu_1_stop);
  and and_1 (and_1_out, clk, or_1_out);
  Multiplexer #(.width(32)) multiplexer_1 (.in0(multiplexer_4_out), .in1(in_1), .out(multiplexer_1_out), .sel(reset));
  Register #(.width(32)) register_1 (.D(multiplexer_1_out), .clk(and_1_out), .Q(register_1_q));  // open: en, clr
  Add4 add4_1 (.pcin(register_1_q), .pcout(add4_1_pcout));
  ROM #(.addrWidth(14), .dataWidth(32)) rom_1 (.addr(register_1_q[15:2]), .data(rom_1_data));
  Multiplexer #(.width(5)) multiplexer_2 (
    .in0(rom_1_data[20:16]), .in1(rom_1_data[15:11]), .out(multiplexer_2_out), .sel(cu_1_regdst));
  Count count_1 (
    .reset(reset), .clk(and_1_out),
    .result({count_1_result_4, count_1_result_3, count_1_result_2, count_1_result}));
  Hex_Digit_Display hex_digit_display_1 (.value(count_1_result_4));  // open: dp
  Hex_Digit_Display hex_digit_display_2 (.value(count_1_result_3));  // open: dp
  Hex_Digit_Display hex_digit_display_3 (.value(count_1_result_2));  // open: dp
  Hex_Digit_Display hex_digit_display_4 (.value(count_1_result));  // open: dp
  CU cu_1 (
    .opcode(rom_1_data[31:26]), .RegDst(cu_1_regdst), .ALUop(cu_1_aluop), .ALUSrc(cu_1_alusrc),
    .Branch(cu_1_branch), .MemRead(cu_1_memread), .Memwrite(cu_1_memwrite), .Regwrite(cu_1_regwrite),
    .MemtoReg(cu_1_memtoreg), .EXtop(cu_1_extop), .stop(cu_1_stop));
  MIPS_32x32_reg mips_32x32_reg_1 (
    .raddr1(rom_1_data[25:21]), .raddr2(rom_1_data[20:16]), .wen(cu_1_regwrite), .wdata(multiplexer_5_out),
    .waddr(multiplexer_2_out), .clk(and_1_out), .rdata1(mips_32x32_reg_1_rdata1),
    .rdata2(mips_32x32_reg_1_rdata2));
  EX_control ex_control_1 (.Imm_in(rom_1_data[15:0]), .EXop(cu_1_extop), .Imm_out(ex_control_1_imm_out));
  Multiplexer #(.width(32)) multiplexer_3 (
    .in0(mips_32x32_reg_1_rdata2), .in1(ex_control_1_imm_out), .out(multiplexer_3_out), .sel(cu_1_alusrc));
  shift_left_2 shift_left_2_1 (.in_1(ex_control_1_imm_out), .out_2(shift_left_2_1_out_2));
  and and_2 (and_2_out, cu_1_branch, not_2_out);
  not not_2 (not_2_out, alu_1_zero);
  ALU alu_1 (
    .source1(mips_32x32_reg_1_rdata1), .source2(multiplexer_3_out), .alu_control(alu_control_1_alucontrol),
    .zero(alu_1_zero), .result(alu_1_result));
  ALU_control alu_control_1 (.ALUop(cu_1_aluop), .func(rom_1_data[5:0]), .ALUcontrol(alu_control_1_alucontrol));
  Adder #(.width(32)) adder_1 (.a(add4_1_pcout), .b(shift_left_2_1_out_2), .out(adder_1_out));  // open: cin, cout
  Multiplexer #(.width(32)) multiplexer_4 (
    .in0(add4_1_pcout), .in1(adder_1_out), .out(multiplexer_4_out), .sel(and_2_out));
  RAM #(.addrWidth(14), .asyncread("true"), .dataWidth(32)) ram_1 (
    .addr(alu_1_result[15:2]), .we(cu_1_memwrite), .oe(cu_1_memread), .clk(and_1_out),
    .din(mips_32x32_reg_1_rdata2), .dout(ram_1_dout));
  Multiplexer #(.width(32)) multiplexer_5 (
    .in0(alu_1_result), .in1(ram_1_dout), .out(multiplexer_5_out), .sel(cu_1_memtoreg));

  // Notes on the sheet:
  //   contents of rom_1 (hex, n*v repeats v):
  //   8c010000 ac010004 fc000000 ac010008
endmodule

module ALU (
  input  [31:0] source1,
  input  [31:0] source2,
  input  [2:0] alu_control,
  output zero,
  output [31:0] result
);

  wire comparator_1_lt;
  wire [31:0] adder_1_out, bit_extender_1_out, or_1_out, shifter_1_out, subtractor_1_out;

  Adder #(.width(32)) adder_1 (.a(source1), .b(source2), .out(adder_1_out), .cin(1'b0));  // open: cout
  Subtractor #(.width(32)) subtractor_1 (.a(source1), .b(source2), .out(subtractor_1_out), .bin(1'b0));  // open: bout
  assign or_1_out = source1 | source2;  // OR_Gate or_1, 32 bits wide
  Comparator #(.width(32)) comparator_1 (.a(source1), .b(source2), .lt(comparator_1_lt));  // open: gt, eq
  Shifter #(.width(32)) shifter_1 (.in(source2), .\dist (5'b10000), .out(shifter_1_out));
  assign bit_extender_1_out = {{31{1'b0}}, comparator_1_lt};  // Bit_Extender bit_extender_1
  Multiplexer #(.select(3), .width(32)) multiplexer_1 (
    .in0(adder_1_out), .in1(subtractor_1_out), .in2(or_1_out), .in3(bit_extender_1_out), .in4(shifter_1_out),
    .out(result), .sel(alu_control));  // open: in5, in6, in7
  Comparator #(.width(32)) comparator_2 (.a(result), .b({32{1'b0}}), .eq(zero));  // open: gt, lt
endmodule

module CU (
  input  [5:0] opcode,
  output RegDst,
  output [2:0] ALUop,
  output ALUSrc,
  output Branch,
  output MemRead,
  output Memwrite,
  output Regwrite,
  output MemtoReg,
  output EXtop,
  output stop
);

  wire comparator_3_eq;

  Comparator #(.width(6)) comparator_1 (.a({6{1'b0}}), .b(opcode), .eq(RegDst));  // open: gt, lt
  Comparator #(.width(6)) comparator_2 (.a(6'b001111), .b(opcode), .eq(ALUop[2]));  // open: gt, lt
  Comparator #(.width(6)) comparator_3 (.a(6'b001101), .b(opcode), .eq(comparator_3_eq));  // open: gt, lt
  Comparator #(.width(6)) comparator_4 (.a(6'b000101), .b(opcode), .eq(Branch));  // open: gt, lt
  Comparator #(.width(6)) comparator_5 (.a(6'b100011), .b(opcode), .eq(MemRead));  // open: gt, lt
  Comparator #(.width(6)) comparator_6 (.a(6'b101011), .b(opcode), .eq(Memwrite));  // open: gt, lt
  Comparator #(.width(6)) comparator_7 (.a({6{1'b1}}), .b(opcode), .eq(stop));  // open: gt, lt
  or or_1 (ALUSrc, Memwrite, ALUop[2], comparator_3_eq, MemRead);
  or or_2 (EXtop, MemRead, Memwrite, Branch);
  or or_3 (Regwrite, RegDst, MemRead, ALUop[2], comparator_3_eq);
  or or_4 (ALUop[1], RegDst, comparator_3_eq);
  or or_5 (ALUop[0], comparator_3_eq, Branch);

  assign MemtoReg = MemRead;

  // Notes on the sheet:
  //   R_type
  //   LUI
  //   ORI
  //   BNE
  //   LW
  //   SW
  //   STP
endmodule

module ALU_control (
  input  [2:0] ALUop,
  input  [5:0] func,
  output [2:0] ALUcontrol
);

  wire and_1_out, and_3_out, and_4_out, and_5_out, and_6_out, comparator_1_eq, comparator_2_eq,
       comparator_3_eq, not_1_out, not_2_out, not_3_out;

  not not_1 (not_1_out, ALUop[2]);
  Comparator #(.width(6)) comparator_1 (.a(func), .b(6'b100001), .eq(comparator_1_eq));  // open: gt, lt
  Comparator #(.width(6)) comparator_2 (.a(func), .b(6'b100010), .eq(comparator_2_eq));  // open: gt, lt
  Comparator #(.width(6)) comparator_3 (.a(func), .b(6'b101010), .eq(comparator_3_eq));  // open: gt, lt
  not not_2 (not_2_out, ALUop[0]);
  and and_1 (and_1_out, not_2_out, ALUop[1], not_1_out);
  // AND_Gate and_2 has open pins: in0=and_1_out, in1=comparator_1_eq, out=open
  and and_3 (and_3_out, comparator_2_eq, and_1_out);
  and and_4 (and_4_out, comparator_3_eq, and_1_out);
  and and_5 (and_5_out, ALUop[0], not_3_out);
  not not_3 (not_3_out, ALUop[1]);
  or or_1 (ALUcontrol[0], and_5_out, and_3_out, and_4_out);
  and and_6 (and_6_out, ALUop[0], ALUop[1]);
  or or_2 (ALUcontrol[1], and_6_out, and_4_out);

  assign ALUcontrol[2] = ALUop[2];

  // Notes on the sheet:
  //   is_add
  //   is_sub
  //   is_slt
endmodule

module Add4 (
  input  [31:0] pcin,
  output [31:0] pcout
);

  Adder #(.width(32)) adder_1 (.a(pcin), .b(32'h4), .out(pcout));  // open: cin, cout
endmodule

module group_0 (
  input  cp,
  input  group_en,
  input  [31:0] wdata,
  input  [2:0] inner_waddr,
  output [31:0] reg_0,
  output [31:0] reg_1,
  output [31:0] reg_2,
  output [31:0] reg_3,
  output [31:0] reg_4,
  output [31:0] reg_5,
  output [31:0] reg_6,
  output [31:0] reg_7
);

  wire and_1_out, and_2_out, and_3_out, and_4_out, and_5_out, and_6_out, and_7_out, not_1_out, not_2_out,
       not_3_out, not_4_out, not_5_out, not_6_out, not_7_out, not_8_out, not_9_out;
  wire [31:0] multiplexer_1_out, multiplexer_2_out, multiplexer_3_out, multiplexer_4_out, multiplexer_5_out,
       multiplexer_6_out, multiplexer_7_out;

  Multiplexer #(.width(32)) multiplexer_1 (.in0(reg_1), .in1(wdata), .out(multiplexer_1_out), .sel(and_1_out));
  Multiplexer #(.width(32)) multiplexer_2 (.in0(reg_2), .in1(wdata), .out(multiplexer_2_out), .sel(and_2_out));
  Multiplexer #(.width(32)) multiplexer_3 (.in0(reg_3), .in1(wdata), .out(multiplexer_3_out), .sel(and_3_out));
  Multiplexer #(.width(32)) multiplexer_4 (.in0(reg_4), .in1(wdata), .out(multiplexer_4_out), .sel(and_4_out));
  Multiplexer #(.width(32)) multiplexer_5 (.in0(reg_5), .in1(wdata), .out(multiplexer_5_out), .sel(and_5_out));
  Multiplexer #(.width(32)) multiplexer_6 (.in0(reg_6), .in1(wdata), .out(multiplexer_6_out), .sel(and_6_out));
  Multiplexer #(.width(32)) multiplexer_7 (.in0(reg_7), .in1(wdata), .out(multiplexer_7_out), .sel(and_7_out));
  not not_1 (not_1_out, inner_waddr[1]);
  not not_2 (not_2_out, inner_waddr[2]);
  not not_3 (not_3_out, inner_waddr[0]);
  not not_4 (not_4_out, inner_waddr[2]);
  not not_5 (not_5_out, inner_waddr[2]);
  not not_6 (not_6_out, inner_waddr[0]);
  not not_7 (not_7_out, inner_waddr[1]);
  not not_8 (not_8_out, inner_waddr[1]);
  not not_9 (not_9_out, inner_waddr[0]);
  and and_1 (and_1_out, inner_waddr[0], not_1_out, not_2_out);
  and and_2 (and_2_out, not_3_out, inner_waddr[1], not_4_out);
  and and_3 (and_3_out, inner_waddr[0], inner_waddr[1], not_5_out);
  and and_4 (and_4_out, not_6_out, not_7_out, inner_waddr[2]);
  and and_5 (and_5_out, inner_waddr[0], not_8_out, inner_waddr[2]);
  and and_6 (and_6_out, not_9_out, inner_waddr[1], inner_waddr[2]);
  and and_7 (and_7_out, inner_waddr[0], inner_waddr[1], inner_waddr[2]);
  Register #(.width(32)) register_1 (.D({32{1'b0}}), .en(group_en), .clk(cp), .Q(reg_0));  // open: clr
  Register #(.width(32)) register_2 (.D(multiplexer_1_out), .en(group_en), .clk(cp), .Q(reg_1));  // open: clr
  Register #(.width(32)) register_3 (.D(multiplexer_2_out), .en(group_en), .clk(cp), .Q(reg_2));  // open: clr
  Register #(.width(32)) register_4 (.D(multiplexer_3_out), .en(group_en), .clk(cp), .Q(reg_3));  // open: clr
  Register #(.width(32)) register_5 (.D(multiplexer_4_out), .en(group_en), .clk(cp), .Q(reg_4));  // open: clr
  Register #(.width(32)) register_6 (.D(multiplexer_5_out), .en(group_en), .clk(cp), .Q(reg_5));  // open: clr
  Register #(.width(32)) register_7 (.D(multiplexer_6_out), .en(group_en), .clk(cp), .Q(reg_6));  // open: clr
  Register #(.width(32)) register_8 (.D(multiplexer_7_out), .en(group_en), .clk(cp), .Q(reg_7));  // open: clr
endmodule

module MIPS_32x32_reg (
  input  [4:0] raddr1,
  input  [4:0] raddr2,
  input  wen,
  input  [31:0] wdata,
  input  [4:0] waddr,
  input  clk,
  output [31:0] rdata1,
  output [31:0] rdata2
);

  wire and_1_out, and_2_out, and_3_out, and_4_out, not_1_out, not_2_out, not_3_out, not_4_out;
  wire [31:0] group_0_1_reg_0, group_0_1_reg_1, group_0_1_reg_2, group_0_1_reg_3, group_0_1_reg_4,
       group_0_1_reg_5, group_0_1_reg_6, group_0_1_reg_7, group_123_1_reg_0, group_123_1_reg_1,
       group_123_1_reg_2, group_123_1_reg_3, group_123_1_reg_4, group_123_1_reg_5, group_123_1_reg_6,
       group_123_1_reg_7, group_123_2_reg_0, group_123_2_reg_1, group_123_2_reg_2, group_123_2_reg_3,
       group_123_2_reg_4, group_123_2_reg_5, group_123_2_reg_6, group_123_2_reg_7, group_123_3_reg_0,
       group_123_3_reg_1, group_123_3_reg_2, group_123_3_reg_3, group_123_3_reg_4, group_123_3_reg_5,
       group_123_3_reg_6, group_123_3_reg_7, multiplexer_1_out, multiplexer_2_out, multiplexer_3_out,
       multiplexer_4_out, multiplexer_5_out, multiplexer_6_out, multiplexer_7_out, multiplexer_8_out;

  not not_1 (not_1_out, waddr[3]);
  and and_1 (and_1_out, wen, not_1_out, not_2_out);
  not not_2 (not_2_out, waddr[4]);
  and and_2 (and_2_out, wen, waddr[3], not_3_out);
  not not_3 (not_3_out, waddr[4]);
  not not_4 (not_4_out, waddr[3]);
  and and_3 (and_3_out, wen, not_4_out, waddr[4]);
  and and_4 (and_4_out, waddr[3], waddr[4], wen);
  group_0 group_0_1 (
    .cp(clk), .group_en(and_1_out), .wdata(wdata), .inner_waddr(waddr[2:0]), .reg_0(group_0_1_reg_0),
    .reg_1(group_0_1_reg_1), .reg_2(group_0_1_reg_2), .reg_3(group_0_1_reg_3), .reg_4(group_0_1_reg_4),
    .reg_5(group_0_1_reg_5), .reg_6(group_0_1_reg_6), .reg_7(group_0_1_reg_7));
  group_123 group_123_1 (
    .cp(clk), .group_en(and_2_out), .wdata(wdata), .inner_waddr(waddr[2:0]), .reg_0(group_123_1_reg_0),
    .reg_1(group_123_1_reg_1), .reg_2(group_123_1_reg_2), .reg_3(group_123_1_reg_3),
    .reg_4(group_123_1_reg_4), .reg_5(group_123_1_reg_5), .reg_6(group_123_1_reg_6), .reg_7(group_123_1_reg_7));
  group_123 group_123_2 (
    .cp(clk), .group_en(and_3_out), .wdata(wdata), .inner_waddr(waddr[2:0]), .reg_0(group_123_2_reg_0),
    .reg_1(group_123_2_reg_1), .reg_2(group_123_2_reg_2), .reg_3(group_123_2_reg_3),
    .reg_4(group_123_2_reg_4), .reg_5(group_123_2_reg_5), .reg_6(group_123_2_reg_6), .reg_7(group_123_2_reg_7));
  group_123 group_123_3 (
    .cp(clk), .group_en(and_4_out), .wdata(wdata), .inner_waddr(waddr[2:0]), .reg_0(group_123_3_reg_0),
    .reg_1(group_123_3_reg_1), .reg_2(group_123_3_reg_2), .reg_3(group_123_3_reg_3),
    .reg_4(group_123_3_reg_4), .reg_5(group_123_3_reg_5), .reg_6(group_123_3_reg_6), .reg_7(group_123_3_reg_7));
  Multiplexer #(.select(3), .width(32)) multiplexer_1 (
    .in0(group_0_1_reg_0), .in1(group_0_1_reg_1), .in2(group_0_1_reg_2), .in3(group_0_1_reg_3),
    .in4(group_0_1_reg_4), .in5(group_0_1_reg_5), .in6(group_0_1_reg_6), .in7(group_0_1_reg_7),
    .out(multiplexer_1_out), .sel(raddr1[2:0]));
  Multiplexer #(.select(3), .width(32)) multiplexer_2 (
    .in0(group_123_1_reg_0), .in1(group_123_1_reg_1), .in2(group_123_1_reg_2), .in3(group_123_1_reg_3),
    .in4(group_123_1_reg_4), .in5(group_123_1_reg_5), .in6(group_123_1_reg_6), .in7(group_123_1_reg_7),
    .out(multiplexer_2_out), .sel(raddr1[2:0]));
  Multiplexer #(.select(3), .width(32)) multiplexer_3 (
    .in0(group_123_2_reg_0), .in1(group_123_2_reg_1), .in2(group_123_2_reg_2), .in3(group_123_2_reg_3),
    .in4(group_123_2_reg_4), .in5(group_123_2_reg_5), .in6(group_123_2_reg_6), .in7(group_123_2_reg_7),
    .out(multiplexer_3_out), .sel(raddr1[2:0]));
  Multiplexer #(.select(3), .width(32)) multiplexer_4 (
    .in0(group_123_3_reg_0), .in1(group_123_3_reg_1), .in2(group_123_3_reg_2), .in3(group_123_3_reg_3),
    .in4(group_123_3_reg_4), .in5(group_123_3_reg_5), .in6(group_123_3_reg_6), .in7(group_123_3_reg_7),
    .out(multiplexer_4_out), .sel(raddr1[2:0]));
  Multiplexer #(.select(3), .width(32)) multiplexer_5 (
    .in0(group_0_1_reg_0), .in1(group_0_1_reg_1), .in2(group_0_1_reg_2), .in3(group_0_1_reg_3),
    .in4(group_0_1_reg_4), .in5(group_0_1_reg_5), .in6(group_0_1_reg_6), .in7(group_0_1_reg_7),
    .out(multiplexer_5_out), .sel(raddr2[2:0]));
  Multiplexer #(.select(3), .width(32)) multiplexer_6 (
    .in0(group_123_1_reg_0), .in1(group_123_1_reg_1), .in2(group_123_1_reg_2), .in3(group_123_1_reg_3),
    .in4(group_123_1_reg_4), .in5(group_123_1_reg_5), .in6(group_123_1_reg_6), .in7(group_123_1_reg_7),
    .out(multiplexer_6_out), .sel(raddr2[2:0]));
  Multiplexer #(.select(3), .width(32)) multiplexer_7 (
    .in0(group_123_2_reg_0), .in1(group_123_2_reg_1), .in2(group_123_2_reg_2), .in3(group_123_2_reg_3),
    .in4(group_123_2_reg_4), .in5(group_123_2_reg_5), .in6(group_123_2_reg_6), .in7(group_123_2_reg_7),
    .out(multiplexer_7_out), .sel(raddr2[2:0]));
  Multiplexer #(.select(3), .width(32)) multiplexer_8 (
    .in0(group_123_3_reg_0), .in1(group_123_3_reg_1), .in2(group_123_3_reg_2), .in3(group_123_3_reg_3),
    .in4(group_123_3_reg_4), .in5(group_123_3_reg_5), .in6(group_123_3_reg_6), .in7(group_123_3_reg_7),
    .out(multiplexer_8_out), .sel(raddr2[2:0]));
  Multiplexer #(.select(2), .width(32)) multiplexer_9 (
    .in0(multiplexer_1_out), .in1(multiplexer_2_out), .in2(multiplexer_3_out), .in3(multiplexer_4_out),
    .out(rdata1), .sel(raddr1[4:3]));
  Multiplexer #(.select(2), .width(32)) multiplexer_10 (
    .in0(multiplexer_5_out), .in1(multiplexer_6_out), .in2(multiplexer_7_out), .in3(multiplexer_8_out),
    .out(rdata2), .sel(raddr2[4:3]));
endmodule

module group_123 (
  input  cp,
  input  group_en,
  input  [31:0] wdata,
  input  [2:0] inner_waddr,
  output [31:0] reg_0,
  output [31:0] reg_1,
  output [31:0] reg_2,
  output [31:0] reg_3,
  output [31:0] reg_4,
  output [31:0] reg_5,
  output [31:0] reg_6,
  output [31:0] reg_7
);

  wire and_1_out, and_2_out, and_3_out, and_4_out, and_5_out, and_6_out, and_7_out, and_8_out, not_1_out,
       not_2_out, not_3_out, not_4_out, not_5_out, not_6_out, not_7_out, not_8_out, not_9_out, not_10_out,
       not_11_out, not_12_out;
  wire [31:0] multiplexer_1_out, multiplexer_2_out, multiplexer_3_out, multiplexer_4_out, multiplexer_5_out,
       multiplexer_6_out, multiplexer_7_out, multiplexer_8_out;

  Multiplexer #(.width(32)) multiplexer_1 (.in0(reg_0), .in1(wdata), .out(multiplexer_1_out), .sel(and_1_out));
  Multiplexer #(.width(32)) multiplexer_2 (.in0(reg_1), .in1(wdata), .out(multiplexer_2_out), .sel(and_2_out));
  Multiplexer #(.width(32)) multiplexer_3 (.in0(reg_2), .in1(wdata), .out(multiplexer_3_out), .sel(and_3_out));
  Multiplexer #(.width(32)) multiplexer_4 (.in0(reg_3), .in1(wdata), .out(multiplexer_4_out), .sel(and_4_out));
  Multiplexer #(.width(32)) multiplexer_5 (.in0(reg_4), .in1(wdata), .out(multiplexer_5_out), .sel(and_5_out));
  Multiplexer #(.width(32)) multiplexer_6 (.in0(reg_5), .in1(wdata), .out(multiplexer_6_out), .sel(and_6_out));
  Multiplexer #(.width(32)) multiplexer_7 (.in0(reg_6), .in1(wdata), .out(multiplexer_7_out), .sel(and_7_out));
  Multiplexer #(.width(32)) multiplexer_8 (.in0(reg_7), .in1(wdata), .out(multiplexer_8_out), .sel(and_8_out));
  not not_1 (not_1_out, inner_waddr[0]);
  not not_2 (not_2_out, inner_waddr[1]);
  not not_3 (not_3_out, inner_waddr[2]);
  not not_4 (not_4_out, inner_waddr[1]);
  not not_5 (not_5_out, inner_waddr[2]);
  not not_6 (not_6_out, inner_waddr[0]);
  not not_7 (not_7_out, inner_waddr[2]);
  not not_8 (not_8_out, inner_waddr[2]);
  not not_9 (not_9_out, inner_waddr[1]);
  not not_10 (not_10_out, inner_waddr[0]);
  and and_1 (and_1_out, not_1_out, not_2_out, not_3_out);
  and and_2 (and_2_out, inner_waddr[0], not_4_out, not_5_out);
  and and_3 (and_3_out, not_6_out, inner_waddr[1], not_7_out);
  and and_4 (and_4_out, inner_waddr[0], inner_waddr[1], not_8_out);
  not not_11 (not_11_out, inner_waddr[0]);
  not not_12 (not_12_out, inner_waddr[1]);
  and and_5 (and_5_out, not_11_out, not_12_out, inner_waddr[2]);
  and and_6 (and_6_out, inner_waddr[0], not_9_out, inner_waddr[2]);
  and and_7 (and_7_out, not_10_out, inner_waddr[1], inner_waddr[2]);
  and and_8 (and_8_out, inner_waddr[0], inner_waddr[1], inner_waddr[2]);
  Register #(.width(32)) register_1 (.D(multiplexer_1_out), .en(group_en), .clk(cp), .Q(reg_0));  // open: clr
  Register #(.width(32)) register_2 (.D(multiplexer_2_out), .en(group_en), .clk(cp), .Q(reg_1));  // open: clr
  Register #(.width(32)) register_3 (.D(multiplexer_3_out), .en(group_en), .clk(cp), .Q(reg_2));  // open: clr
  Register #(.width(32)) register_4 (.D(multiplexer_4_out), .en(group_en), .clk(cp), .Q(reg_3));  // open: clr
  Register #(.width(32)) register_5 (.D(multiplexer_5_out), .en(group_en), .clk(cp), .Q(reg_4));  // open: clr
  Register #(.width(32)) register_6 (.D(multiplexer_6_out), .en(group_en), .clk(cp), .Q(reg_5));  // open: clr
  Register #(.width(32)) register_7 (.D(multiplexer_7_out), .en(group_en), .clk(cp), .Q(reg_6));  // open: clr
  Register #(.width(32)) register_8 (.D(multiplexer_8_out), .en(group_en), .clk(cp), .Q(reg_7));  // open: clr
endmodule

module shift_left_2 (
  input  [31:0] in_1,
  output [31:0] out_2
);


  assign out_2 = {in_1[29:0], 2'b00};
endmodule

module EX_control (
  input  [15:0] Imm_in,
  input  EXop,
  output [31:0] Imm_out
);

  wire [31:0] bit_extender_1_out, bit_extender_2_out;

  assign bit_extender_1_out = {{16{1'b0}}, Imm_in};  // Bit_Extender bit_extender_1
  assign bit_extender_2_out = {{16{Imm_in[15]}}, Imm_in};  // Bit_Extender bit_extender_2
  Multiplexer #(.width(32)) multiplexer_1 (
    .in0(bit_extender_1_out), .in1(bit_extender_2_out), .out(Imm_out), .sel(EXop));
endmodule

module Count (
  input  reset,
  input  clk,
  output [15:0] result
);

  wire [15:0] adder_1_out;

  Register #(.width(16)) register_1 (.D(adder_1_out), .clk(clk), .Q(result), .clr(reset));  // open: en
  Adder #(.width(16)) adder_1 (.a(result), .b(16'h1), .out(adder_1_out));  // open: cin, cout
endmodule
