// Logisim project 4.2-流水线CPU.circ as structural Verilog: 18 circuits, main circuit main
module main (
  input  [15:0] in_1,
  input  [31:0] in_2,
  input  reset,
  input  clk
);

  wire alu_1_zero, alu_2_zero, and_1_out, and_2_out, and_3_out, comparator_1_eq, cu_1_extop, hazard_1_stall,
       not_1_out, not_2_out, not_3_out, not_4_out, or_1_out;
  wire [1:0] exmem_1_aluout_putout, forwarding_controla_1_c2, forwarding_controlb_1_c2;
  wire [2:0] alu_control_1_alucontrol, alu_control_2_alucontrol, cu_1_aluop;
  wire [3:0] count_1_result_2, count_1_result_3;
  wire [4:0] exmem_1_regdst_out, idex_1_regdst_out, idex_1_rs_out, idex_1_rt_out, memwb_1_regdst_out,
       multiplexer_6_out;
  wire [5:0] idex_1_func_out;
  wire [9:9] exmem_1_control_out_2, memwb_1_control_out_2;
  wire [10:0] cu_1_stop;
  wire [13:0] exmem_1_aluout_putout_2;
  wire [14:0] exmem_1_control_out, memwb_1_control_out;
  wire [15:0] count_1_result, exmem_1_aluout_putout_3, idex_1_control_out, multiplexer_7_out;
  wire [31:0] add4_1_pcout, adder_1_out, alu_2_result, ex_control_1_imm_out, exmem_1_rttomem_out,
       idex_1_alusrc1_out, idex_1_alusrc2_out, idex_1_imm_out, ifid_1_instruct_out, ifid_1_npc_out,
       memwb_1_aluout_putout, memwb_1_lmdata_out, mips_32x32_reg_1_rdata1, mips_32x32_reg_1_rdata2,
       multiplexer_1_out, multiplexer_2_out, multiplexer_3_out, multiplexer_4_out, multiplexer_5_out,
       multiplexer_8_out, multiplexer_9_out, multiplexer_10_out, multiplexer_11_out, ram_1_dout,
       register_1_q, rom_1_data, shift_left_2_1_out_2;

  or or_1 (or_1_out, reset, not_1_out);
  not not_1 (not_1_out, memwb_1_control_out[0]);
  Multiplexer #(.width(32)) multiplexer_1 (.in0(multiplexer_2_out), .in1(in_2), .out(multiplexer_1_out), .sel(reset));
  and and_1 (and_1_out, not_2_out, not_3_out);
  and and_2 (and_2_out, clk, or_1_out);
  Register #(.width(32)) register_1 (
    .D(multiplexer_1_out), .en(and_1_out), .clk(and_2_out), .Q(register_1_q), .clr(reset));
  not not_2 (not_2_out, comparator_1_eq);
  ROM #(.addrWidth(14), .dataWidth(32)) rom_1 (.addr(register_1_q[15:2]), .data(rom_1_data));
  Multiplexer #(.width(32)) multiplexer_2 (
    .in0(add4_1_pcout), .in1(adder_1_out), .out(multiplexer_2_out), .sel(and_3_out));
  Add4 add4_1 (.pcin(register_1_q), .pcout(add4_1_pcout));
  Hex_Digit_Display hex_digit_display_1 (.value(count_1_result_3));  // open: dp
  Hex_Digit_Display hex_digit_display_2 (.value(count_1_result[15:12]));  // open: dp
  Hex_Digit_Display hex_digit_display_3 (.value(count_1_result_2));  // open: dp
  Hex_Digit_Display hex_digit_display_4 (.value(count_1_result[3:0]));  // open: dp
  Count count_1 (
    .reset(reset), .clk(and_2_out),
    .result({count_1_result[15:12], count_1_result_3, count_1_result_2, count_1_result[3:0]}));
  not not_3 (not_3_out, hazard_1_stall);
  Multiplexer #(.width(32)) multiplexer_3 (
    .in0(rom_1_data), .in1({32{1'b0}}), .out(multiplexer_3_out), .sel(and_3_out));
  Comparator #(.width(32)) comparator_1 (
    .a(multiplexer_3_out), .b(32'hfc000000), .eq(comparator_1_eq));  // open: gt, lt
  IFID ifid_1 (
    .ID_BLock(hazard_1_stall), .NPC_IN(add4_1_pcout), .instruct_In(multiplexer_3_out), .reset(reset),
    .clk(and_2_out), .NPC_OUT(ifid_1_npc_out), .instruct_out(ifid_1_instruct_out));
  Hazard hazard_1 (
    .IDEXMemRead(idex_1_control_out[7]), .IDEX_RT(idex_1_rt_out), .IFID_Rs(ifid_1_instruct_out[25:21]),
    .IFID_Rt(ifid_1_instruct_out[20:16]), .EXMEMM_rt(exmem_1_regdst_out),
    .EXMEMM_Memread(exmem_1_control_out[7]), .stall(hazard_1_stall));
  CU cu_1 (
    .opcode(ifid_1_instruct_out[31:26]), .MemtoReg(cu_1_stop[10]), .Regwrite(cu_1_stop[9]),
    .Memwrite(cu_1_stop[8]), .MemRead(cu_1_stop[7]), .Branch(cu_1_stop[6]), .ALUSrc(cu_1_stop[5]),
    .ALUop(cu_1_aluop), .RegDst(cu_1_stop[1]), .stop(cu_1_stop[0]), .EXtop(cu_1_extop));
  MIPS_32x32_reg mips_32x32_reg_1 (
    .raddr1(ifid_1_instruct_out[25:21]), .raddr2(ifid_1_instruct_out[20:16]), .wen(memwb_1_control_out_2[9]),
    .wdata(multiplexer_11_out), .waddr(memwb_1_regdst_out), .clk(and_2_out), .reset(reset),
    .rdata1(mips_32x32_reg_1_rdata1), .rdata2(mips_32x32_reg_1_rdata2));
  EX_control ex_control_1 (.Imm_in(ifid_1_instruct_out[15:0]), .EXop(cu_1_extop), .Imm_out(ex_control_1_imm_out));
  Multiplexer #(.select(2), .width(32)) multiplexer_4 (
    .in0(mips_32x32_reg_1_rdata1), .in1(multiplexer_11_out), .in2(alu_2_result), .out(multiplexer_4_out),
    .sel(forwarding_controla_1_c2));  // open: in3
  Multiplexer #(.select(2), .width(32)) multiplexer_5 (
    .in0(mips_32x32_reg_1_rdata2), .in1(multiplexer_11_out), .in2(alu_2_result), .out(multiplexer_5_out),
    .sel(forwarding_controlb_1_c2));  // open: in3
  Multiplexer #(.width(5)) multiplexer_6 (
    .in0(ifid_1_instruct_out[20:16]), .in1(ifid_1_instruct_out[15:11]), .out(multiplexer_6_out),
    .sel(cu_1_stop[1]));
  LED led_1 (.in(cu_1_stop[0]));
  shift_left_2 shift_left_2_1 (.in_1(ex_control_1_imm_out), .out_2(shift_left_2_1_out_2));
  Forwarding_controlA forwarding_controla_1 (
    .IDEX_Rs(idex_1_rs_out), .EXMEM_rd(exmem_1_regdst_out), .EXMEM_regw(exmem_1_control_out_2[9]),
    .MEMWB_rd(memwb_1_regdst_out), .MEMWB_regw(memwb_1_control_out_2[9]), .c1(forwarding_controla_1_c2[1]),
    .c2(forwarding_controla_1_c2[0]));
  Forwarding_controlB forwarding_controlb_1 (
    .IDEX_Rt(idex_1_rt_out), .EXMEM_rd(exmem_1_regdst_out), .EXMEM_regw(exmem_1_control_out_2[9]),
    .MEMWB_rd(memwb_1_regdst_out), .MEMWB_regw(memwb_1_control_out_2[9]), .c1(forwarding_controlb_1_c2[1]),
    .c2(forwarding_controlb_1_c2[0]));
  Adder #(.width(32)) adder_1 (.a(ifid_1_npc_out), .b(shift_left_2_1_out_2), .out(adder_1_out));  // open: cin, cout
  Multiplexer #(.width(16)) multiplexer_7 (
    .in0({{5{1'b0}}, cu_1_stop[10:5], cu_1_aluop, cu_1_stop[1:0]}), .in1(in_1), .out(multiplexer_7_out),
    .sel(hazard_1_stall));
  ALU_control alu_control_1 (
    .ALUop(cu_1_aluop), .func(ifid_1_instruct_out[5:0]), .ALUcontrol(alu_control_1_alucontrol));
  and and_3 (and_3_out, not_4_out, cu_1_stop[6]);
  not not_4 (not_4_out, alu_1_zero);
  ALU alu_1 (
    .source1(multiplexer_4_out), .source2(multiplexer_5_out), .alu_control(alu_control_1_alucontrol),
    .zero(alu_1_zero));  // open: result
  IDEX idex_1 (
    .IDEX_rs(ifid_1_instruct_out[25:21]), .control_in(multiplexer_7_out),
    .ALUsrc1_in(mips_32x32_reg_1_rdata1), .ALUsrc2_in(mips_32x32_reg_1_rdata2),
    .Imm_in(ex_control_1_imm_out), .RegDst_in(multiplexer_6_out), .IDEX_Rt(ifid_1_instruct_out[20:16]),
    .func_in(ifid_1_instruct_out[5:0]), .reset(reset), .clk(and_2_out), .RS_out(idex_1_rs_out),
    .control_out(idex_1_control_out), .ALUsrc1_out(idex_1_alusrc1_out), .ALUsrc2_out(idex_1_alusrc2_out),
    .imm_out(idex_1_imm_out), .RegDst_out(idex_1_regdst_out), .RT_out(idex_1_rt_out),
    .func_out(idex_1_func_out));  // open: nnno, nooooo
  Multiplexer #(.select(2), .width(32)) multiplexer_8 (
    .in0(idex_1_alusrc1_out), .in1(multiplexer_11_out),
    .in2({exmem_1_aluout_putout_3, exmem_1_aluout_putout_2, exmem_1_aluout_putout}), .out(multiplexer_8_out),
    .sel(forwarding_controla_1_c2));  // open: in3
  Multiplexer #(.select(2), .width(32)) multiplexer_9 (
    .in0(idex_1_alusrc2_out), .in1(multiplexer_11_out),
    .in2({exmem_1_aluout_putout_3, exmem_1_aluout_putout_2, exmem_1_aluout_putout}), .out(multiplexer_9_out),
    .sel(forwarding_controlb_1_c2));  // open: in3
  Multiplexer #(.width(32)) multiplexer_10 (
    .in0(multiplexer_9_out), .in1(idex_1_imm_out), .out(multiplexer_10_out), .sel(idex_1_control_out[5]));
  LED led_2 (.in(idex_1_control_out[0]));
  ALU alu_2 (
    .source1(multiplexer_8_out), .source2(multiplexer_10_out), .alu_control(alu_control_2_alucontrol),
    .zero(alu_2_zero), .result(alu_2_result));
  ALU_control alu_control_2 (
    .ALUop(idex_1_control_out[4:2]), .func(idex_1_func_out), .ALUcontrol(alu_control_2_alucontrol));
  EXMEM exmem_1 (
    .control_in({idex_1_control_out[15:6], {5{1'b0}}, idex_1_control_out[0]}), .noo(alu_2_zero),
    .ALUout_putin(alu_2_result), .RTtoMem_in(multiplexer_9_out), .RegDst_in(idex_1_regdst_out),
    .reset(reset), .clk(and_2_out),
    .control_out({exmem_1_control_out[14:9], exmem_1_control_out_2[9], exmem_1_control_out[8:0]}),
    .ALUout_putout({exmem_1_aluout_putout_3, exmem_1_aluout_putout_2, exmem_1_aluout_putout}),
    .RTtoMem_out(exmem_1_rttomem_out), .RegDst_out(exmem_1_regdst_out));  // open: nononono, nonono, nonon, no
  LED led_3 (.in(exmem_1_control_out[0]));
  RAM #(.addrWidth(14), .asyncread("true"), .dataWidth(32)) ram_1 (
    .addr(exmem_1_aluout_putout_2), .we(exmem_1_control_out[8]), .oe(exmem_1_control_out[7]),
    .clk(and_2_out), .din(exmem_1_rttomem_out), .dout(ram_1_dout));
  MEMWB memwb_1 (
    .control_in({exmem_1_control_out[14:9], exmem_1_control_out_2[9], {8{1'b0}}, exmem_1_control_out[0]}),
    .LMData_in(ram_1_dout),
    .ALUout_putin({exmem_1_aluout_putout_3, exmem_1_aluout_putout_2, exmem_1_aluout_putout}),
    .RegDst_in(exmem_1_regdst_out), .reset(reset), .clk(and_2_out), .ALUout_putout(memwb_1_aluout_putout),
    .LMdata_out(memwb_1_lmdata_out),
    .control_out({memwb_1_control_out[14:9], memwb_1_control_out_2[9], memwb_1_control_out[8:0]}),
    .RegDst_out(memwb_1_regdst_out));  // open: NULLll3
  Multiplexer #(.width(32)) multiplexer_11 (
    .in0(memwb_1_aluout_putout), .in1(memwb_1_lmdata_out), .out(multiplexer_11_out),
    .sel(memwb_1_control_out[9]));
  LED led_4 (.in(memwb_1_control_out[0]));

  // Notes on the sheet:
  //   contents of rom_1 (hex, n*v repeats v):
  //   34010001 34020001 34070004 34050100 3c080000 1053021 221821 34410000 34620000 ad020000 8d040000
  //   14440003 1074021 106482a 1520fff7 fc000000 14c0fff5
endmodule

module ALU (
  input  [31:0] source1,
  input  [31:0] source2,
  input  [2:0] alu_control,
  output zero,
  output [31:0] result
);

  wire comparator_1_lt;
  wire [31:0] adder_1_out, bit_extender_1_out, or_1_out, shifter_1_out, subtractor_1_out;

  Adder #(.width(32)) adder_1 (.a(source1), .b(source2), .out(adder_1_out), .cin(1'b0));  // open: cout
  Subtractor #(.width(32)) subtractor_1 (.a(source1), .b(source2), .out(subtractor_1_out), .bin(1'b0));  // open: bout
  assign or_1_out = source1 | source2;  // OR_Gate or_1, 32 bits wide
  Comparator #(.width(32)) comparator_1 (.a(source1), .b(source2), .lt(comparator_1_lt));  // open: gt, eq
  Shifter #(.width(32)) shifter_1 (.in(source2), .\dist (5'b10000), .out(shifter_1_out));
  assign bit_extender_1_out = {{31{1'b0}}, comparator_1_lt};  // Bit_Extender bit_extender_1
  Multiplexer #(.select(3), .width(32)) multiplexer_1 (
    .in0(adder_1_out), .in1(subtractor_1_out), .in2(or_1_out), .in3(bit_extender_1_out), .in4(shifter_1_out),
    .out(result), .sel(alu_control));  // open: in5, in6, in7
  Comparator #(.width(32)) comparator_2 (.a(result), .b({32{1'b0}}), .eq(zero));  // open: gt, lt
endmodule

module CU (
  input  [5:0] opcode,
  output MemtoReg,
  output Regwrite,
  output Memwrite,
  output MemRead,
  output Branch,
  output ALUSrc,
  output [2:0] ALUop,
  output RegDst,
  output stop,
  output EXtop
);

  wire comparator_3_eq;

  Comparator #(.width(6)) comparator_1 (.a({6{1'b0}}), .b(opcode), .eq(RegDst));  // open: gt, lt
  Comparator #(.width(6)) comparator_2 (.a(6'b001111), .b(opcode), .eq(ALUop[2]));  // open: gt, lt
  Comparator #(.width(6)) comparator_3 (.a(6'b001101), .b(opcode), .eq(comparator_3_eq));  // open: gt, lt
  Comparator #(.width(6)) comparator_4 (.a(6'b000101), .b(opcode), .eq(Branch));  // open: gt, lt
  Comparator #(.width(6)) comparator_5 (.a(6'b100011), .b(opcode), .eq(MemRead));  // open: gt, lt
  Comparator #(.width(6)) comparator_6 (.a(6'b101011), .b(opcode), .eq(Memwrite));  // open: gt, lt
  Comparator #(.width(6)) comparator_7 (.a({6{1'b1}}), .b(opcode), .eq(stop));  // open: gt, lt
  or or_1 (ALUSrc, Memwrite, ALUop[2], comparator_3_eq, MemRead);
  or or_2 (EXtop, MemRead, Memwrite, Branch);
  or or_3 (Regwrite, RegDst, MemRead, ALUop[2], comparator_3_eq);
  or or_4 (ALUop[1], RegDst, comparator_3_eq);
  or or_5 (ALUop[0], comparator_3_eq, Branch);

  assign MemtoReg = MemRead;

  // Notes on the sheet:
  //   R_type
  //   LUI
  //   ORI
  //   BNE
  //   LW
  //   SW
  //   STP
endmodule

module ALU_control (
  input  [2:0] ALUop,
  input  [5:0] func,
  output [2:0] ALUcontrol
);

  wire and_1_out, and_3_out, and_4_out, and_5_out, and_6_out, comparator_1_eq, comparator_2_eq,
       comparator_3_eq, not_1_out, not_2_out, not_3_out;

  not not_1 (not_1_out, ALUop[2]);
  Comparator #(.width(6)) comparator_1 (.a(func), .b(6'b100001), .eq(comparator_1_eq));  // open: gt, lt
  Comparator #(.width(6)) comparator_2 (.a(func), .b(6'b100010), .eq(comparator_2_eq));  // open: gt, lt
  Comparator #(.width(6)) comparator_3 (.a(func), .b(6'b101010), .eq(comparator_3_eq));  // open: gt, lt
  not not_2 (not_2_out, ALUop[0]);
  and and_1 (and_1_out, not_2_out, ALUop[1], not_1_out);
  // AND_Gate and_2 has open pins: in0=and_1_out, in1=comparator_1_eq, out=open
  and and_3 (and_3_out, comparator_2_eq, and_1_out);
  and and_4 (and_4_out, comparator_3_eq, and_1_out);
  and and_5 (and_5_out, ALUop[0], not_3_out);
  not not_3 (not_3_out, ALUop[1]);
  or or_1 (ALUcontrol[0], and_5_out, and_3_out, and_4_out);
  and and_6 (and_6_out, ALUop[0], ALUop[1]);
  or or_2 (ALUcontrol[1], and_6_out, and_4_out);

  assign ALUcontrol[2] = ALUop[2];

  // Notes on the sheet:
  //   is_add
  //   is_sub
  //   is_slt
endmodule

module Add4 (
  input  [31:0] pcin,
  output [31:0] pcout
);

  Adder #(.width(32)) adder_1 (.a(pcin), .b(32'h4), .out(pcout));  // open: cin, cout
endmodule

module group_0 (
  input  cp,
  input  group_en,
  input  [31:0] wdata,
  input  [2:0] inner_waddr,
  input  reset,
  output [31:0] reg_0,
  output [31:0] reg_1,
  output [31:0] reg_2,
  output [31:0] reg_3,
  output [31:0] reg_4,
  output [31:0] reg_5,
  output [31:0] reg_6,
  output [31:0] reg_7
);

  wire and_1_out, and_2_out, and_3_out, and_4_out, and_5_out, and_6_out, and_7_out, not_1_out, not_2_out,
       not_3_out, not_4_out, not_5_out, not_6_out, not_7_out, not_8_out, not_9_out;
  wire [31:0] multiplexer_1_out, multiplexer_2_out, multiplexer_3_out, multiplexer_4_out, multiplexer_5_out,
       multiplexer_6_out, multiplexer_7_out;

  Multiplexer #(.width(32)) multiplexer_1 (.in0(reg_1), .in1(wdata), .out(multiplexer_1_out), .sel(and_1_out));
  Multiplexer #(.width(32)) multiplexer_2 (.in0(reg_2), .in1(wdata), .out(multiplexer_2_out), .sel(and_2_out));
  Multiplexer #(.width(32)) multiplexer_3 (.in0(reg_3), .in1(wdata), .out(multiplexer_3_out), .sel(and_3_out));
  Multiplexer #(.width(32)) multiplexer_4 (.in0(reg_4), .in1(wdata), .out(multiplexer_4_out), .sel(and_4_out));
  Multiplexer #(.width(32)) multiplexer_5 (.in0(reg_5), .in1(wdata), .out(multiplexer_5_out), .sel(and_5_out));
  Multiplexer #(.width(32)) multiplexer_6 (.in0(reg_6), .in1(wdata), .out(multiplexer_6_out), .sel(and_6_out));
  Multiplexer #(.width(32)) multiplexer_7 (.in0(reg_7), .in1(wdata), .out(multiplexer_7_out), .sel(and_7_out));
  not not_1 (not_1_out, inner_waddr[1]);
  not not_2 (not_2_out, inner_waddr[2]);
  not not_3 (not_3_out, inner_waddr[0]);
  not not_4 (not_4_out, inner_waddr[2]);
  not not_5 (not_5_out, inner_waddr[2]);
  not not_6 (not_6_out, inner_waddr[0]);
  not not_7 (not_7_out, inner_waddr[1]);
  not not_8 (not_8_out, inner_waddr[1]);
  not not_9 (not_9_out, inner_waddr[0]);
  and and_1 (and_1_out, inner_waddr[0], not_1_out, not_2_out);
  and and_2 (and_2_out, not_3_out, inner_waddr[1], not_4_out);
  and and_3 (and_3_out, inner_waddr[0], inner_waddr[1], not_5_out);
  and and_4 (and_4_out, not_6_out, not_7_out, inner_waddr[2]);
  and and_5 (and_5_out, inner_waddr[0], not_8_out, inner_waddr[2]);
  and and_6 (and_6_out, not_9_out, inner_waddr[1], inner_waddr[2]);
  and and_7 (and_7_out, inner_waddr[0], inner_waddr[1], inner_waddr[2]);
  Register #(.width(32)) register_1 (.D({32{1'b0}}), .en(group_en), .clk(cp), .Q(reg_0), .clr(reset));
  Register #(.width(32)) register_2 (.D(multiplexer_1_out), .en(group_en), .clk(cp), .Q(reg_1), .clr(reset));
  Register #(.width(32)) register_3 (.D(multiplexer_2_out), .en(group_en), .clk(cp), .Q(reg_2), .clr(reset));
  Register #(.width(32)) register_4 (.D(multiplexer_3_out), .en(group_en), .clk(cp), .Q(reg_3), .clr(reset));
  Register #(.width(32)) register_5 (.D(multiplexer_4_out), .en(group_en), .clk(cp), .Q(reg_4), .clr(reset));
  Register #(.width(32)) register_6 (.D(multiplexer_5_out), .en(group_en), .clk(cp), .Q(reg_5), .clr(reset));
  Register #(.width(32)) register_7 (.D(multiplexer_6_out), .en(group_en), .clk(cp), .Q(reg_6), .clr(reset));
  Register #(.width(32)) register_8 (.D(multiplexer_7_out), .en(group_en), .clk(cp), .Q(reg_7), .clr(reset));
endmodule

module MIPS_32x32_reg (
  input  [4:0] raddr1,
  input  [4:0] raddr2,
  input  wen,
  input  [31:0] wdata,
  input  [4:0] waddr,
  input  clk,
  input  reset,
  output [31:0] rdata1,
  output [31:0] rdata2
);

  wire and_1_out, and_2_out, and_3_out, and_4_out, and_5_out, and_6_out, comparator_1_eq, comparator_2_eq,
       not_1_out, not_2_out, not_3_out, not_4_out;
  wire [31:0] group_0_1_reg_0, group_0_1_reg_1, group_0_1_reg_2, group_0_1_reg_3, group_0_1_reg_4,
       group_0_1_reg_5, group_0_1_reg_6, group_0_1_reg_7, group_123_1_reg_0, group_123_1_reg_1,
       group_123_1_reg_2, group_123_1_reg_3, group_123_1_reg_4, group_123_1_reg_5, group_123_1_reg_6,
       group_123_1_reg_7, group_123_2_reg_0, group_123_2_reg_1, group_123_2_reg_2, group_123_2_reg_3,
       group_123_2_reg_4, group_123_2_reg_5, group_123_2_reg_6, group_123_2_reg_7, group_123_3_reg_0,
       group_123_3_reg_1, group_123_3_reg_2, group_123_3_reg_3, group_123_3_reg_4, group_123_3_reg_5,
       group_123_3_reg_6, group_123_3_reg_7, multiplexer_1_out, multiplexer_2_out, multiplexer_3_out,
       multiplexer_4_out, multiplexer_5_out, multiplexer_6_out, multiplexer_7_out, multiplexer_8_out,
       multiplexer_9_out, multiplexer_10_out;

  not not_1 (not_1_out, waddr[3]);
  and and_1 (and_1_out, wen, not_1_out, not_2_out);
  not not_2 (not_2_out, waddr[4]);
  and and_2 (and_2_out, wen, waddr[3], not_3_out);
  not not_3 (not_3_out, waddr[4]);
  not not_4 (not_4_out, waddr[3]);
  and and_3 (and_3_out, wen, not_4_out, waddr[4]);
  and and_4 (and_4_out, waddr[3], waddr[4], wen);
  Comparator #(.width(5)) comparator_1 (.a(raddr1), .b(waddr), .eq(comparator_1_eq));  // open: gt, lt
  Comparator #(.width(5)) comparator_2 (.a(raddr2), .b(waddr), .eq(comparator_2_eq));  // open: gt, lt
  and and_5 (and_5_out, comparator_1_eq, wen);
  and and_6 (and_6_out, comparator_2_eq, wen);
  group_0 group_0_1 (
    .cp(clk), .group_en(and_1_out), .wdata(wdata), .inner_waddr(waddr[2:0]), .reset(reset),
    .reg_0(group_0_1_reg_0), .reg_1(group_0_1_reg_1), .reg_2(group_0_1_reg_2), .reg_3(group_0_1_reg_3),
    .reg_4(group_0_1_reg_4), .reg_5(group_0_1_reg_5), .reg_6(group_0_1_reg_6), .reg_7(group_0_1_reg_7));
  group_123 group_123_1 (
    .cp(clk), .group_en(and_2_out), .wdata(wdata), .inner_waddr(waddr[2:0]), .reg_0(group_123_1_reg_0),
    .reg_1(group_123_1_reg_1), .reg_2(group_123_1_reg_2), .reg_3(group_123_1_reg_3),
    .reg_4(group_123_1_reg_4), .reg_5(group_123_1_reg_5), .reg_6(group_123_1_reg_6), .reg_7(group_123_1_reg_7));
  group_123 group_123_2 (
    .cp(clk), .group_en(and_3_out), .wdata(wdata), .inner_waddr(waddr[2:0]), .reg_0(group_123_2_reg_0),
    .reg_1(group_123_2_reg_1), .reg_2(group_123_2_reg_2), .reg_3(group_123_2_reg_3),
    .reg_4(group_123_2_reg_4), .reg_5(group_123_2_reg_5), .reg_6(group_123_2_reg_6), .reg_7(group_123_2_reg_7));
  group_123 group_123_3 (
    .cp(clk), .group_en(and_4_out), .wdata(wdata), .inner_waddr(waddr[2:0]), .reg_0(group_123_3_reg_0),
    .reg_1(group_123_3_reg_1), .reg_2(group_123_3_reg_2), .reg_3(group_123_3_reg_3),
    .reg_4(group_123_3_reg_4), .reg_5(group_123_3_reg_5), .reg_6(group_123_3_reg_6), .reg_7(group_123_3_reg_7));
  Multiplexer #(.select(3), .width(32)) multiplexer_1 (
    .in0(group_0_1_reg_0), .in1(group_0_1_reg_1), .in2(group_0_1_reg_2), .in3(group_0_1_reg_3),
    .in4(group_0_1_reg_4), .in5(group_0_1_reg_5), .in6(group_0_1_reg_6), .in7(group_0_1_reg_7),
    .out(multiplexer_1_out), .sel(raddr1[2:0]));
  Multiplexer #(.select(3), .width(32)) multiplexer_2 (
    .in0(group_123_1_reg_0), .in1(group_123_1_reg_1), .in2(group_123_1_reg_2), .in3(group_123_1_reg_3),
    .in4(group_123_1_reg_4), .in5(group_123_1_reg_5), .in6(group_123_1_reg_6), .in7(group_123_1_reg_7),
    .out(multiplexer_2_out), .sel(raddr1[2:0]));
  Multiplexer #(.select(3), .width(32)) multiplexer_3 (
    .in0(group_123_2_reg_0), .in1(group_123_2_reg_1), .in2(group_123_2_reg_2), .in3(group_123_2_reg_3),
    .in4(group_123_2_reg_4), .in5(group_123_2_reg_5), .in6(group_123_2_reg_6), .in7(group_123_2_reg_7),
    .out(multiplexer_3_out), .sel(raddr1[2:0]));
  Multiplexer #(.select(3), .width(32)) multiplexer_4 (
    .in0(group_123_3_reg_0), .in1(group_123_3_reg_1), .in2(group_123_3_reg_2), .in3(group_123_3_reg_3),
    .in4(group_123_3_reg_4), .in5(group_123_3_reg_5), .in6(group_123_3_reg_6), .in7(group_123_3_reg_7),
    .out(multiplexer_4_out), .sel(raddr1[2:0]));
  Multiplexer #(.select(3), .width(32)) multiplexer_5 (
    .in0(group_0_1_reg_0), .in1(group_0_1_reg_1), .in2(group_0_1_reg_2), .in3(group_0_1_reg_3),
    .in4(group_0_1_reg_4), .in5(group_0_1_reg_5), .in6(group_0_1_reg_6), .in7(group_0_1_reg_7),
    .out(multiplexer_5_out), .sel(raddr2[2:0]));
  Multiplexer #(.select(3), .width(32)) multiplexer_6 (
    .in0(group_123_1_reg_0), .in1(group_123_1_reg_1), .in2(group_123_1_reg_2), .in3(group_123_1_reg_3),
    .in4(group_123_1_reg_4), .in5(group_123_1_reg_5), .in6(group_123_1_reg_6), .in7(group_123_1_reg_7),
    .out(multiplexer_6_out), .sel(raddr2[2:0]));
  Multiplexer #(.select(3), .width(32)) multiplexer_7 (
    .in0(group_123_2_reg_0), .in1(group_123_2_reg_1), .in2(group_123_2_reg_2), .in3(group_123_2_reg_3),
    .in4(group_123_2_reg_4), .in5(group_123_2_reg_5), .in6(group_123_2_reg_6), .in7(group_123_2_reg_7),
    .out(multiplexer_7_out), .sel(raddr2[2:0]));
  Multiplexer #(.select(3), .width(32)) multiplexer_8 (
    .in0(group_123_3_reg_0), .in1(group_123_3_reg_1), .in2(group_123_3_reg_2), .in3(group_123_3_reg_3),
    .in4(group_123_3_reg_4), .in5(group_123_3_reg_5), .in6(group_123_3_reg_6), .in7(group_123_3_reg_7),
    .out(multiplexer_8_out), .sel(raddr2[2:0]));
  Multiplexer #(.select(2), .width(32)) multiplexer_9 (
    .in0(multiplexer_1_out), .in1(multiplexer_2_out), .in2(multiplexer_3_out), .in3(multiplexer_4_out),
    .out(multiplexer_9_out), .sel(raddr1[4:3]));
  Multiplexer #(.select(2), .width(32)) multiplexer_10 (
    .in0(multiplexer_5_out), .in1(multiplexer_6_out), .in2(multiplexer_7_out), .in3(multiplexer_8_out),
    .out(multiplexer_10_out), .sel(raddr2[4:3]));
  Multiplexer #(.width(32)) multiplexer_11 (.in0(multiplexer_9_out), .in1(wdata), .out(rdata1), .sel(and_5_out));
  Multiplexer #(.width(32)) multiplexer_12 (.in0(multiplexer_10_out), .in1(wdata), .out(rdata2), .sel(and_6_out));
endmodule

module group_123 (
  input  cp,
  input  group_en,
  input  [31:0] wdata,
  input  [2:0] inner_waddr,
  output [31:0] reg_0,
  output [31:0] reg_1,
  output [31:0] reg_2,
  output [31:0] reg_3,
  output [31:0] reg_4,
  output [31:0] reg_5,
  output [31:0] reg_6,
  output [31:0] reg_7
);

  wire and_1_out, and_2_out, and_3_out, and_4_out, and_5_out, and_6_out, and_7_out, and_8_out, not_1_out,
       not_2_out, not_3_out, not_4_out, not_5_out, not_6_out, not_7_out, not_8_out, not_9_out, not_10_out,
       not_11_out, not_12_out;
  wire [31:0] multiplexer_1_out, multiplexer_2_out, multiplexer_3_out, multiplexer_4_out, multiplexer_5_out,
       multiplexer_6_out, multiplexer_7_out, multiplexer_8_out;

  Multiplexer #(.width(32)) multiplexer_1 (.in0(reg_0), .in1(wdata), .out(multiplexer_1_out), .sel(and_1_out));
  Multiplexer #(.width(32)) multiplexer_2 (.in0(reg_1), .in1(wdata), .out(multiplexer_2_out), .sel(and_2_out));
  Multiplexer #(.width(32)) multiplexer_3 (.in0(reg_2), .in1(wdata), .out(multiplexer_3_out), .sel(and_3_out));
  Multiplexer #(.width(32)) multiplexer_4 (.in0(reg_3), .in1(wdata), .out(multiplexer_4_out), .sel(and_4_out));
  Multiplexer #(.width(32)) multiplexer_5 (.in0(reg_4), .in1(wdata), .out(multiplexer_5_out), .sel(and_5_out));
  Multiplexer #(.width(32)) multiplexer_6 (.in0(reg_5), .in1(wdata), .out(multiplexer_6_out), .sel(and_6_out));
  Multiplexer #(.width(32)) multiplexer_7 (.in0(reg_6), .in1(wdata), .out(multiplexer_7_out), .sel(and_7_out));
  Multiplexer #(.width(32)) multiplexer_8 (.in0(reg_7), .in1(wdata), .out(multiplexer_8_out), .sel(and_8_out));
  not not_1 (not_1_out, inner_waddr[0]);
  not not_2 (not_2_out, inner_waddr[1]);
  not not_3 (not_3_out, inner_waddr[2]);
  not not_4 (not_4_out, inner_waddr[1]);
  not not_5 (not_5_out, inner_waddr[2]);
  not not_6 (not_6_out, inner_waddr[0]);
  not not_7 (not_7_out, inner_waddr[2]);
  not not_8 (not_8_out, inner_waddr[2]);
  not not_9 (not_9_out, inner_waddr[1]);
  not not_10 (not_10_out, inner_waddr[0]);
  and and_1 (and_1_out, not_1_out, not_2_out, not_3_out);
  and and_2 (and_2_out, inner_waddr[0], not_4_out, not_5_out);
  and and_3 (and_3_out, not_6_out, inner_waddr[1], not_7_out);
  and and_4 (and_4_out, inner_waddr[0], inner_waddr[1], not_8_out);
  not not_11 (not_11_out, inner_waddr[0]);
  not not_12 (not_12_out, inner_waddr[1]);
  and and_5 (and_5_out, not_11_out, not_12_out, inner_waddr[2]);
  and and_6 (and_6_out, inner_waddr[0], not_9_out, inner_waddr[2]);
  and and_7 (and_7_out, not_10_out, inner_waddr[1], inner_waddr[2]);
  and and_8 (and_8_out, inner_waddr[0], inner_waddr[1], inner_waddr[2]);
  Register #(.width(32)) register_1 (.D(multiplexer_1_out), .en(group_en), .clk(cp), .Q(reg_0));  // open: clr
  Register #(.width(32)) register_2 (.D(multiplexer_2_out), .en(group_en), .clk(cp), .Q(reg_1));  // open: clr
  Register #(.width(32)) register_3 (.D(multiplexer_3_out), .en(group_en), .clk(cp), .Q(reg_2));  // open: clr
  Register #(.width(32)) register_4 (.D(multiplexer_4_out), .en(group_en), .clk(cp), .Q(reg_3));  // open: clr
  Register #(.width(32)) register_5 (.D(multiplexer_5_out), .en(group_en), .clk(cp), .Q(reg_4));  // open: clr
  Register #(.width(32)) register_6 (.D(multiplexer_6_out), .en(group_en), .clk(cp), .Q(reg_5));  // open: clr
  Register #(.width(32)) register_7 (.D(multiplexer_7_out), .en(group_en), .clk(cp), .Q(reg_6));  // open: clr
  Register #(.width(32)) register_8 (.D(multiplexer_8_out), .en(group_en), .clk(cp), .Q(reg_7));  // open: clr
endmodule

module shift_left_2 (
  input  [31:0] in_1,
  output [31:0] out_2
);


  assign out_2 = {in_1[29:0], 2'b00};
endmodule

module EX_control (
  input  [15:0] Imm_in,
  input  EXop,
  output [31:0] Imm_out
);

  wire [31:0] bit_extender_1_out, bit_extender_2_out;

  assign bit_extender_1_out = {{16{1'b0}}, Imm_in};  // Bit_Extender bit_extender_1
  assign bit_extender_2_out = {{16{Imm_in[15]}}, Imm_in};  // Bit_Extender bit_extender_2
  Multiplexer #(.width(32)) multiplexer_1 (
    .in0(bit_extender_1_out), .in1(bit_extender_2_out), .out(Imm_out), .sel(EXop));
endmodule

module Count (
  input  reset,
  input  clk,
  output [15:0] result
);

  wire [15:0] adder_1_out;

  Register #(.width(16)) register_1 (.D(adder_1_out), .clk(clk), .Q(result), .clr(reset));  // open: en
  Adder #(.width(16)) adder_1 (.a(result), .b(16'h1), .out(adder_1_out));  // open: cin, cout
endmodule

module IFID (
  input  ID_BLock,
  input  [31:0] NPC_IN,
  input  [31:0] instruct_In,
  input  reset,
  input  clk,
  output [31:0] NPC_OUT,
  output [31:0] instruct_out
);

  wire not_1_out;

  not not_1 (not_1_out, ID_BLock);
  Register #(.width(32)) Reg_NPC (.D(NPC_IN), .en(not_1_out), .clk(clk), .Q(NPC_OUT), .clr(reset));
  Register #(.width(32)) Reg_Inst (.D(instruct_In), .en(not_1_out), .clk(clk), .Q(instruct_out), .clr(reset));
endmodule

module EXMEM (
  input  nononono,
  input  [31:0] nonono,
  input  [15:0] control_in,
  input  noo,
  input  [31:0] ALUout_putin,
  input  [31:0] RTtoMem_in,
  input  [4:0] RegDst_in,
  input  reset,
  input  clk,
  output [31:0] nonon,
  output [15:0] control_out,
  output no,
  output [31:0] ALUout_putout,
  output [31:0] RTtoMem_out,
  output [4:0] RegDst_out
);

  Register #(.width(32)) register_1 (.D(nonono), .en(1'b1), .clk(clk), .Q(nonon), .clr(reset));
  Register #(.width(16)) register_2 (.D(control_in), .en(1'b1), .clk(clk), .Q(control_out), .clr(reset));
  Register #(.width(1)) register_3 (.D(noo), .en(1'b1), .clk(clk), .Q(no), .clr(reset));
  Register #(.width(32)) register_4 (.D(ALUout_putin), .en(1'b1), .clk(clk), .Q(ALUout_putout), .clr(reset));
  Register #(.width(5)) register_5 (.D(RegDst_in), .en(1'b1), .clk(clk), .Q(RegDst_out), .clr(reset));
  Register #(.width(32)) register_6 (.D(RTtoMem_in), .en(1'b1), .clk(clk), .Q(RTtoMem_out), .clr(reset));
endmodule

module IDEX (
  input  nnno,
  input  [4:0] IDEX_rs,
  input  [15:0] control_in,
  input  [31:0] ALUsrc1_in,
  input  [31:0] ALUsrc2_in,
  input  [31:0] Imm_in,
  input  [4:0] RegDst_in,
  input  [4:0] IDEX_Rt,
  input  [5:0] func_in,
  input  reset,
  input  clk,
  output [4:0] RS_out,
  output [15:0] control_out,
  output [31:0] ALUsrc1_out,
  output [31:0] ALUsrc2_out,
  output [31:0] imm_out,
  output [4:0] RegDst_out,
  output [4:0] RT_out,
  output [5:0] func_out,
  output nooooo
);

  Register #(.width(5)) register_1 (.D(IDEX_rs), .en(1'b1), .clk(clk), .Q(RS_out), .clr(reset));
  Register #(.width(16)) register_2 (.D(control_in), .en(1'b1), .clk(clk), .Q(control_out), .clr(reset));
  Register #(.width(32)) register_3 (.D(ALUsrc1_in), .en(1'b1), .clk(clk), .Q(ALUsrc1_out), .clr(reset));
  Register #(.width(32)) register_4 (.D(ALUsrc2_in), .en(1'b1), .clk(clk), .Q(ALUsrc2_out), .clr(reset));
  Register #(.width(32)) register_5 (.D(Imm_in), .en(1'b1), .clk(clk), .Q(imm_out), .clr(reset));
  Register #(.width(5)) register_6 (.D(RegDst_in), .en(1'b1), .clk(clk), .Q(RegDst_out), .clr(reset));
  Register #(.width(5)) register_7 (.D(IDEX_Rt), .en(1'b1), .clk(clk), .Q(RT_out), .clr(reset));
  Register #(.width(6)) register_8 (.D(func_in), .en(1'b1), .clk(clk), .Q(func_out), .clr(reset));
endmodule

module MEMWB (
  input  NULLll3,
  input  [15:0] control_in,
  input  [31:0] LMData_in,
  input  [31:0] ALUout_putin,
  input  [4:0] RegDst_in,
  input  reset,
  input  clk,
  output [31:0] ALUout_putout,
  output [31:0] LMdata_out,
  output [15:0] control_out,
  output [4:0] RegDst_out
);

  wire not_1_out;

  not not_1 (not_1_out, NULLll3);
  Register #(.width(16)) register_1 (.D(control_in), .en(not_1_out), .clk(clk), .Q(control_out), .clr(reset));
  Register #(.width(32)) register_2 (.D(LMData_in), .en(not_1_out), .clk(clk), .Q(LMdata_out), .clr(reset));
  Register #(.width(32)) register_3 (.D(ALUout_putin), .en(not_1_out), .clk(clk), .Q(ALUout_putout));  // open: clr
  Register #(.width(5)) register_4 (.D(RegDst_in), .en(not_1_out), .clk(clk), .Q(RegDst_out), .clr(reset));
endmodule

module Forwarding_controlA (
  input  [4:0] IDEX_Rs,
  input  [4:0] EXMEM_rd,
  input  EXMEM_regw,
  input  [4:0] MEMWB_rd,
  input  MEMWB_regw,
  output c1,
  output c2
);

  wire and_1_out, comparator_1_eq, comparator_2_eq, comparator_3_eq, comparator_4_eq, not_1_out, not_2_out,
       not_3_out;

  Comparator #(.width(5)) comparator_1 (.a(IDEX_Rs), .b(EXMEM_rd), .eq(comparator_1_eq));  // open: gt, lt
  not not_1 (not_1_out, comparator_2_eq);
  Comparator #(.width(5)) comparator_2 (.a(EXMEM_rd), .b({5{1'b0}}), .eq(comparator_2_eq));  // open: gt, lt
  Comparator #(.width(5)) comparator_3 (.a(IDEX_Rs), .b(MEMWB_rd), .eq(comparator_3_eq));  // open: gt, lt
  not not_2 (not_2_out, comparator_4_eq);
  Comparator #(.width(5)) comparator_4 (.a(MEMWB_rd), .b({5{1'b0}}), .eq(comparator_4_eq));  // open: gt, lt
  and and_1 (and_1_out, comparator_3_eq, MEMWB_regw, not_2_out);
  and and_2 (c1, comparator_1_eq, EXMEM_regw, not_1_out);
  not not_3 (not_3_out, c1);
  and and_3 (c2, not_3_out, and_1_out);

  // Notes on the sheet:
  //   Hazard_MEM
  //   Hazard_EX
endmodule

module Hazard (
  input  IDEXMemRead,
  input  [4:0] IDEX_RT,
  input  [4:0] IFID_Rs,
  input  [4:0] IFID_Rt,
  input  [4:0] EXMEMM_rt,
  input  EXMEMM_Memread,
  output stall
);

  wire and_1_out, and_2_out, comparator_1_eq, comparator_2_eq, comparator_3_eq, comparator_4_eq, or_1_out,
       or_2_out;

  Comparator #(.width(5)) comparator_1 (.a(IDEX_RT), .b(IFID_Rs), .eq(comparator_1_eq));  // open: gt, lt
  Comparator #(.width(5)) comparator_2 (.a(IDEX_RT), .b(IFID_Rt), .eq(comparator_2_eq));  // open: gt, lt
  Comparator #(.width(5)) comparator_3 (.a(IDEX_RT), .b(EXMEMM_rt), .eq(comparator_3_eq));  // open: gt, lt
  Comparator #(.width(5)) comparator_4 (.a(IDEX_RT), .b(EXMEMM_rt), .eq(comparator_4_eq));  // open: gt, lt
  or or_1 (or_1_out, comparator_1_eq, comparator_2_eq);
  and and_1 (and_1_out, or_1_out, IDEXMemRead);
  or or_2 (or_2_out, comparator_3_eq, comparator_4_eq);
  and and_2 (and_2_out, or_2_out, EXMEMM_Memread);
  or or_3 (stall, and_1_out, and_2_out);
endmodule

module Forwarding_controlB (
  input  [4:0] IDEX_Rt,
  input  [4:0] EXMEM_rd,
  input  EXMEM_regw,
  input  [4:0] MEMWB_rd,
  input  MEMWB_regw,
  output c1,
  output c2
);

  wire and_1_out, comparator_1_eq, comparator_2_eq, comparator_3_eq, comparator_4_eq, not_1_out, not_2_out,
       not_3_out;

  Comparator #(.width(5)) comparator_1 (.a(IDEX_Rt), .b(EXMEM_rd), .eq(comparator_1_eq));  // open: gt, lt
  not not_1 (not_1_out, comparator_2_eq);
  Comparator #(.width(5)) comparator_2 (.a(EXMEM_rd), .b({5{1'b0}}), .eq(comparator_2_eq));  // open: gt, lt
  Comparator #(.width(5)) comparator_3 (.a(IDEX_Rt), .b(MEMWB_rd), .eq(comparator_3_eq));  // open: gt, lt
  not not_2 (not_2_out, comparator_4_eq);
  Comparator #(.width(5)) comparator_4 (.a(MEMWB_rd), .b({5{1'b0}}), .eq(comparator_4_eq));  // open: gt, lt
  and and_1 (and_1_out, comparator_3_eq, MEMWB_regw, not_2_out);
  and and_2 (c1, comparator_1_eq, EXMEM_regw, not_1_out);
  not not_3 (not_3_out, c1);
  and and_3 (c2, not_3_out, and_1_out);

  // Notes on the sheet:
  //   Hazard_MEM
  //   Hazard_EX
endmodule
